// Logisim project cpu21-riscv.circ as structural Verilog: 22 circuits, main circuit ◇单周期RISC-V
module \重定向流水线  (
  output RegWrite,
  output MemWrite,
  output [31:0] IF_PC,
  output [31:0] ID_PC,
  output [31:0] EX_PC,
  output [31:0] M_PC,
  output [31:0] WB_PC,
  output [31:0] RDin,
  output [31:0] MDin,
  output [31:0] LedData
);

  wire alu_1_equal, and_1_out, and_2_out, and_3_out, and_4_out, and_5_out, and_6_out, and_7_out, BranchTaken,
       CLK, clock_1_out, comparator_1_eq, comparator_1_lt, comparator_2_eq, comparator_2_gt, comparator_3_eq,
       d_ff_1_q, EX_ALU_src, EX_beq, EX_bge, EX_BJump, EX_bne, EX_jal, EX_jalr, EX_JJump, EX_Mem2Reg,
       ex_mem_1_ecall_out, EX_RegWrite, \ex重定向逻辑_1_flush , \ex重定向逻辑_1_loaduse , Go, halt, ID_ALU_src, ID_beq,
       ID_bge, ID_bne, ID_ecall, \id_ex_for_重定向_1_ecall_out , \id_ex_for_重定向_1_lui_out ,
       \id_ex_for_重定向_1_memwrite_out , \id_ex_for_重定向_1_sh_out , ID_jal, ID_jalr, ID_lui, ID_Mem2Reg,
       ID_MemWrite, ID_RegWrite, ID_sh, IR1, IR2, IR3, MEM_lui, MEM_Mem2Reg, MEM_NeedLink, MEM_RegWrite,
       MEM_sh, nand_1_out, not_1_out, not_2_out, not_3_out, not_4_out, not_5_out, or_2_out, or_3_out,
       or_4_out, RST, S, ShiftImm, W1, W2, W3, WB_ecall, \单周期硬布线控制器_1_uret ;
  wire [1:0] \ex重定向逻辑_1_r1_fwd , \ex重定向逻辑_1_r2_fwd , \id_ex_for_重定向_1_r1_fwd_2 , \id_ex_for_重定向_1_r2_fwd_2 ;
  wire [3:0] EX_ALU_op, ID_ALU_op;
  wire [4:0] EX_RegWriteNum, MEM_RegWriteNum, multiplexer_2_out, multiplexer_3_out, WB_RegWriteNum;
  wire [11:0] multiplexer_4_out;
  wire [12:0] CNT_num;
  wire [15:0] \LoadUse次数 , ram_1_data, \总周期数 , \插入气泡数 , \无条件分支数 , \条件分支成功数 ;
  wire [31:0] adder_2_out, adder_3_out, adder_4_out, bit_extender_1_out, bit_extender_2_out,
       bit_extender_3_out, bit_extender_4_out, bit_extender_5_out, EX_ALU_res, EX_BImm, EX_IR, EX_ISImm,
       EX_JImm, ex_mem_1_rs1_out, EX_RS1, EX_RS1_Redirect, EX_RS2, EX_RS2_Redirect,
       \id_ex_for_重定向_1_uimm_out , ID_IR, IF_IR, IF_PC_4, MEM_ALU_res, MEM_IR, MEM_RegData, MEM_RS2,
       MEM_UImm, multiplexer_1_out, multiplexer_5_out, multiplexer_6_out, multiplexer_7_out,
       multiplexer_10_out, multiplexer_13_out, multiplexer_14_out, multiplexer_15_out, regfileforbubble_1_r1,
       regfileforbubble_1_r2, shifter_1_out, shifter_2_out, shifter_3_out, WB_IR, WB_RS1, WB_RS2;
  wire [31:16] ram_1_data_2;

  Button \u_总复位  (.out(RST));
  Button _1 (.out(IR1));
  Button _2 (.out(IR2));
  Button _3 (.out(IR3));
  // Probe on \总周期数 
  // Probe on \总周期数 
  not not_1 (not_1_out, halt);
  and and_1 (and_1_out, not_1_out, not_2_out);
  Register #(.width(32), .trigger("rising"), .Select("low")) PC (
    .D(multiplexer_1_out), .en(and_1_out), .Q(IF_PC), .clk(CLK), .clr(RST));
  Button \u_继续运行  (.out(Go));
  LED #(.active("true")) led_1 (.in(W1));
  LED #(.active("true")) led_2 (.in(W2));
  LED #(.active("true")) led_3 (.in(W3));
  not not_2 (not_2_out, \ex重定向逻辑_1_loaduse );
  Hex_Digit_Display hex_digit_display_1 (.value(LedData[31:28]));  // open: dp
  // Probe on IF_PC[19:0]
  // RiscV_Probe riscv_probe_1: pin names not known; wires that end beside it: IF_IR
  Counter #(.width(16), .max('hffff), .ongoal("wrap"), .trigger("rising"), .behavior("new")) counter_1 (
    .Q(\总周期数 ), .clk(CLK));  // open: load, D, count, carry, clr, preset, down
  Counter #(.width(16), .max('hffff), .ongoal("wrap"), .trigger("rising"), .behavior("new")) counter_2 (
    .Q(\无条件分支数 ), .clk(EX_JJump));  // open: load, D, count, carry, clr, preset, down
  Adder #(.width(32)) adder_1 (.a(32'h4), .b(IF_PC), .out(IF_PC_4), .cin(1'b0));  // open: cout
  Hex_Digit_Display hex_digit_display_2 (.value(LedData[27:24]));  // open: dp
  Hex_Digit_Display hex_digit_display_3 (.value(LedData[23:20]));  // open: dp
  // Probe on ID_PC[19:0]
  // RiscV_Probe riscv_probe_2: pin names not known; wires that end beside it: ID_IR
  and and_2 (and_2_out, not_3_out, \ex重定向逻辑_1_loaduse );
  not not_3 (not_3_out, BranchTaken);
  Hex_Digit_Display hex_digit_display_4 (.value(LedData[19:16]));  // open: dp
  Hex_Digit_Display hex_digit_display_5 (.value(LedData[15:12]));  // open: dp
  Counter #(.width(16), .max('hffff), .ongoal("wrap"), .trigger("rising"), .behavior("new")) counter_3 (
    .Q(\条件分支成功数 ), .clk(EX_BJump));  // open: load, D, count, carry, clr, preset, down
  Counter #(.width(16), .max('hffff), .ongoal("wrap"), .trigger("falling"), .behavior("new")) counter_4 (
    .count(and_2_out), .Q(\LoadUse次数 ), .clk(CLK));  // open: load, D, carry, clr, preset, down
  ROM #(.addrWidth(10), .dataWidth(32), .Select("high")) rom_1 (.addr(IF_PC[11:2]), .data(IF_IR));
  Multiplexer #(.select(1), .width(32), .disabled("Z"), .enable("false")) multiplexer_1 (
    .in0(IF_PC_4), .in1(multiplexer_6_out), .out(multiplexer_1_out), .sel(BranchTaken));
  Hex_Digit_Display hex_digit_display_6 (.value(LedData[11:8]));  // open: dp
  Hex_Digit_Display hex_digit_display_7 (.value(LedData[7:4]));  // open: dp
  // Probe on EX_PC[19:0]
  // RiscV_Probe riscv_probe_3: pin names not known; wires that end beside it: EX_IR
  IF_ID if_id_1 (
    .IRin(IF_IR), .PCin(IF_PC), .CLK(CLK), .IRout(ID_IR), .PCout(ID_PC), .clear(BranchTaken),
    .Stall(\ex重定向逻辑_1_loaduse ), .halt(halt));
  or or_1 (BranchTaken, EX_JJump, EX_BJump);
  Hex_Digit_Display hex_digit_display_8 (.value(LedData[3:0]));  // open: dp
  // Probe on \总周期数 
  // Probe on M_PC[19:0]
  // RiscV_Probe riscv_probe_4: pin names not known; wires that end beside it: MEM_IR
  // Probe on \总周期数 
  // Probe on \无条件分支数 
  // Probe on \条件分支成功数 
  // Probe on \插入气泡数 
  // Probe on \LoadUse次数 
  \单周期硬布线控制器  \u_单周期硬布线控制器_1  (
    .Funct({ID_IR[30], ID_IR[25], ID_IR[14:12]}), .OP(ID_IR[6:2]), .ALU_OP(ID_ALU_op), .MemToReg(ID_Mem2Reg),
    .MemWrite(ID_MemWrite), .ALU_SRC(ID_ALU_src), .ecall(ID_ecall), .bge(ID_bge), .beq(ID_beq), .lui(ID_lui),
    .S_Type(S), .RegWrite(ID_RegWrite), .in_3(ID_IR[21]), .uret(\单周期硬布线控制器_1_uret ), .ShitfImm(ShiftImm),
    .bne(ID_bne), .jalr(ID_jalr), .jal(ID_jal), .sh(ID_sh));  // open: B_Type
  Multiplexer #(.select(1), .width(5), .disabled("Z"), .enable("false")) multiplexer_2 (
    .in0(ID_IR[19:15]), .in1(5'b10001), .out(multiplexer_2_out), .sel(ID_ecall));
  Multiplexer #(.select(1), .width(5), .disabled("Z"), .enable("false")) multiplexer_3 (
    .in0(ID_IR[24:20]), .in1(5'b01010), .out(multiplexer_3_out), .sel(ID_ecall));
  assign bit_extender_1_out = {{27{ID_IR[24]}}, ID_IR[24:20]};  // Bit_Extender bit_extender_1
  assign bit_extender_2_out = {{12{1'b0}}, ID_IR[31:12]};  // Bit_Extender bit_extender_2
  // Probe on IF_PC[11:0]
  // Probe on WB_PC[19:0]
  // RiscV_Probe riscv_probe_5: pin names not known; wires that end beside it: WB_IR
  Multiplexer #(.select(1), .width(12), .disabled("Z"), .enable("false")) multiplexer_4 (
    .in0(ID_IR[31:20]), .in1({ID_IR[31:25], ID_IR[11:7]}), .out(multiplexer_4_out), .sel(S));
  // Probe on EX_PC[11:0]
  // Probe on ID_PC[11:0]
  assign bit_extender_3_out = {{20{multiplexer_4_out[11]}}, multiplexer_4_out};  // Bit_Extender bit_extender_3
  Multiplexer #(.select(1), .width(32), .disabled("Z"), .enable("false")) multiplexer_5 (
    .in0(bit_extender_3_out), .in1(bit_extender_1_out), .out(multiplexer_5_out), .sel(ShiftImm));
  assign bit_extender_4_out = {{20{ID_IR[31]}}, {ID_IR[31], ID_IR[7], ID_IR[30:25], ID_IR[11:8]}};  // Bit_Extender bit_extender_4
  Shifter #(.width(32), .shift("ll")) shifter_1 (.in(bit_extender_2_out), .\dist (5'b01100), .out(shifter_1_out));
  assign bit_extender_5_out = {{12{ID_IR[31]}}, {ID_IR[31], ID_IR[19:12], ID_IR[20], ID_IR[30:21]}};  // Bit_Extender bit_extender_5
  // Probe on M_PC[11:0]
  D_Flip_Flop #(.trigger("high"), .Pre_Clr_Positions("LEGACY"), .NegatePresetClear("false"), .enable("true"), .NewFFLayout("false")) d_ff_1 (.Q(d_ff_1_q));  // open: clk, D, Qn, preset, en, reset
  // Probe on 13'h378
  RegFileForBubble regfileforbubble_1 (
    .Din(RDin), .Clk(CLK), .R1(regfileforbubble_1_r1), .R2(regfileforbubble_1_r2), .WE(RegWrite),
    .W_num(WB_RegWriteNum), .R1_num(multiplexer_2_out), .R2_num(multiplexer_3_out));
  // Probe on WB_PC[11:0]
  Comparator #(.width(13), .mode("twosComplement")) comparator_1 (
    .a(CNT_num), .b(13'h378), .eq(comparator_1_eq), .lt(comparator_1_lt));  // open: gt
  Clock #(.highDuration(1), .lowDuration(1)) clock_1 (.out(clock_1_out));
  nand nand_1 (nand_1_out, d_ff_1_q, comparator_1_eq);
  Counter #(.width(13), .max('h1fff), .ongoal("stay"), .trigger("rising"), .behavior("old")) counter_5 (
    .count(comparator_1_lt), .Q(CNT_num), .clk(clock_1_out));  // open: load, D, carry, clr, preset
  assign CLK = nand_1_out ? clock_1_out : 1'bz;  // Controlled_Buffer controlled_buffer_1
  Pull_Resistor #(.pull(1)) pull_resistor_1 (.node(CLK));
  or or_2 (or_2_out, \ex重定向逻辑_1_flush , \ex重定向逻辑_1_loaduse );
  Multiplexer #(.select(1), .width(32), .disabled("Z"), .enable("false")) multiplexer_6 (
    .in0(multiplexer_7_out), .in1(adder_2_out), .out(multiplexer_6_out), .sel(or_3_out));
  or or_3 (or_3_out, EX_bne, EX_beq, EX_bge);
  \ID_EX_for_重定向  \id_ex_for_重定向_1  (
    .IRin(ID_IR), .PCin(ID_PC), .RS1in(regfileforbubble_1_r1), .RS2in(regfileforbubble_1_r2),
    .Imm_in(multiplexer_5_out), .RegWrite_in(ID_RegWrite), .MemWrite_in(ID_MemWrite),
    .RegWriteNum_in(ID_IR[11:7]), .ALU_src_in(ID_ALU_src), .jal_in(ID_jal), .jalr_in(ID_jalr),
    .beq_in(ID_beq), .bne_in(ID_bne), .bge_in(ID_bge), .sh_in(ID_sh), .lui_in(ID_lui), .ecall_in(ID_ecall),
    .Mem2Reg_in(ID_Mem2Reg), .BImm_in(bit_extender_4_out), .UImm_in(shifter_1_out),
    .JImm_in(bit_extender_5_out), .ALI_op_in(ID_ALU_op), .R1_fwd(\ex重定向逻辑_1_r1_fwd ),
    .R2_fwd(\ex重定向逻辑_1_r2_fwd ), .CLK(CLK), .IRout(EX_IR), .PCout(EX_PC), .RS1out(EX_RS1), .RS2out(EX_RS2),
    .Imm_out(EX_ISImm), .RegWrite_out(EX_RegWrite), .MemWrite_out(\id_ex_for_重定向_1_memwrite_out ),
    .RegWriteNum_out(EX_RegWriteNum), .ALU_src_out(EX_ALU_src), .jal_out(EX_jal), .jalr_out(EX_jalr),
    .beq_out(EX_beq), .bne_out(EX_bne), .bge_out(EX_bge), .sh_out(\id_ex_for_重定向_1_sh_out ),
    .lui_out(\id_ex_for_重定向_1_lui_out ), .ecall_out(\id_ex_for_重定向_1_ecall_out ), .Mem2Reg_out(EX_Mem2Reg),
    .BImm_out(EX_BImm), .UImm_out(\id_ex_for_重定向_1_uimm_out ), .JImm_out(EX_JImm), .ALU_op_out(EX_ALU_op),
    .R1_fwd_2(\id_ex_for_重定向_1_r1_fwd_2 ), .R2_fwd_2(\id_ex_for_重定向_1_r2_fwd_2 ), .halt(halt),
    .clear(or_2_out));
  Multiplexer #(.select(1), .width(32), .disabled("Z"), .enable("false")) multiplexer_7 (
    .in0(adder_3_out), .in1(EX_ALU_res), .out(multiplexer_7_out), .sel(EX_jalr));
  Shifter #(.width(32), .shift("ll")) shifter_2 (.in(EX_BImm), .\dist (5'b00001), .out(shifter_2_out));
  Shifter #(.width(32), .shift("ll")) shifter_3 (.in(EX_JImm), .\dist (5'b00001), .out(shifter_3_out));
  Adder #(.width(32)) adder_2 (.a(shifter_2_out), .b(EX_PC), .out(adder_2_out), .cin(1'b0));  // open: cout
  Adder #(.width(32)) adder_3 (.a(shifter_3_out), .b(EX_PC), .out(adder_3_out), .cin(1'b0));  // open: cout
  \EX重定向逻辑  \ex重定向逻辑_1  (
    .BranchTaken(BranchTaken), .EX_RegWrite(EX_RegWrite), .EX_RegWriteNum(EX_RegWriteNum),
    .MEM_RegWrite(MEM_RegWrite), .MEM_RegWriteNum(MEM_RegWriteNum), .EX_Mem2Reg(EX_Mem2Reg), .ID_IR(ID_IR),
    .R1_fwd(\ex重定向逻辑_1_r1_fwd ), .Flush(\ex重定向逻辑_1_flush ), .R2_fwd(\ex重定向逻辑_1_r2_fwd ),
    .LoadUse(\ex重定向逻辑_1_loaduse ));
  Multiplexer #(.select(2), .width(32), .disabled("Z"), .enable("false")) multiplexer_8 (
    .in0(EX_RS1), .in1(RDin), .in2(MEM_ALU_res), .out(EX_RS1_Redirect), .sel(\id_ex_for_重定向_1_r1_fwd_2 ));  // open: in3
  Multiplexer #(.select(2), .width(32), .disabled("Z"), .enable("false")) multiplexer_9 (
    .in0(EX_RS2), .in1(RDin), .in2(MEM_ALU_res), .out(EX_RS2_Redirect), .sel(\id_ex_for_重定向_1_r2_fwd_2 ));  // open: in3
  Multiplexer #(.select(1), .width(32), .disabled("Z"), .enable("false")) multiplexer_10 (
    .in0(EX_RS2_Redirect), .in1(EX_ISImm), .out(multiplexer_10_out), .sel(EX_ALU_src));
  not not_4 (not_4_out, alu_1_equal);
  and and_3 (and_3_out, not_4_out, EX_bne);
  Comparator #(.width(32), .mode("twosComplement")) comparator_2 (
    .a(EX_RS1_Redirect), .b(EX_RS2), .gt(comparator_2_gt), .eq(comparator_2_eq));  // open: lt
  ALU alu_1 (
    .X(EX_RS1_Redirect), .Y(multiplexer_10_out), .AluOP(EX_ALU_op), .Equal(alu_1_equal), .Result(EX_ALU_res));  // open: Result_2, out_4, out_6
  and and_4 (and_4_out, alu_1_equal, EX_beq);
  or or_4 (or_4_out, comparator_2_gt, comparator_2_eq);
  or or_5 (EX_JJump, EX_jal, EX_jalr);
  or or_6 (EX_BJump, and_4_out, and_3_out, and_5_out);
  and and_5 (and_5_out, EX_bge, or_4_out);
  EX_MEM ex_mem_1 (
    .IR_in(EX_IR), .PC_in(EX_PC), .RS1_in(EX_RS1_Redirect), .RS2_in(EX_RS2_Redirect),
    .UImm_in(\id_ex_for_重定向_1_uimm_out ), .ALU_result_in(EX_ALU_res), .NeedLink_in(EX_JJump),
    .RegWrite_in(EX_RegWrite), .MemWrite_in(\id_ex_for_重定向_1_memwrite_out ), .RegWriteNum_in(EX_RegWriteNum),
    .lui_in(\id_ex_for_重定向_1_lui_out ), .ecall_in(\id_ex_for_重定向_1_ecall_out ),
    .sh_in(\id_ex_for_重定向_1_sh_out ), .Mem2Reg_in(EX_Mem2Reg), .CLK(CLK), .IR_out(MEM_IR), .PC_out(M_PC),
    .RS1_out(ex_mem_1_rs1_out), .RS2_out(MEM_RS2), .UImm_out(MEM_UImm), .ALU_result_out(MEM_ALU_res),
    .NeedLink_out(MEM_NeedLink), .RegWrite_out(MEM_RegWrite), .MemWrite_out(MemWrite),
    .RegWriteNum_out(MEM_RegWriteNum), .lui_out(MEM_lui), .ecall_out(ex_mem_1_ecall_out), .sh_out(MEM_sh),
    .Mem2Reg_out(MEM_Mem2Reg), .halt(halt));
  Multiplexer #(.select(1), .width(32), .disabled("Z"), .enable("false")) multiplexer_11 (
    .in0(MEM_RS2), .in1(multiplexer_13_out), .out(MDin), .sel(MEM_sh));
  Multiplexer #(.select(1), .width(32), .disabled("Z"), .enable("false")) multiplexer_12 (
    .in0(multiplexer_15_out), .in1(adder_4_out), .out(MEM_RegData), .sel(MEM_NeedLink));
  Adder #(.width(32)) adder_4 (.a(32'h4), .b(M_PC), .out(adder_4_out));  // open: cin, cout
  RAM #(.addrWidth(10), .dataWidth(32), .bus("separate"), .Select("high")) ram_1 (
    .addr(MEM_ALU_res[11:2]), .din(MDin), .data({ram_1_data_2, ram_1_data}), .str(MemWrite), .clk(CLK));  // open: sel, ld, clr
  Multiplexer #(.select(1), .width(32), .disabled("Z"), .enable("false")) multiplexer_13 (
    .in0({ram_1_data_2, MEM_RS2[15:0]}), .in1({MEM_RS2[15:0], ram_1_data}), .out(multiplexer_13_out),
    .sel(MEM_ALU_res[1]));
  Multiplexer #(.select(1), .width(32), .disabled("Z"), .enable("false")) multiplexer_14 (
    .in0(MEM_ALU_res), .in1({ram_1_data_2, ram_1_data}), .out(multiplexer_14_out), .sel(MEM_Mem2Reg));
  Multiplexer #(.select(1), .width(32), .disabled("Z"), .enable("false")) multiplexer_15 (
    .in0(multiplexer_14_out), .in1(MEM_UImm), .out(multiplexer_15_out), .sel(MEM_lui));
  MEM_WB mem_wb_1 (
    .IR_in(MEM_IR), .PC_in(M_PC), .RS1_in(ex_mem_1_rs1_out), .RS2_out(MEM_RS2), .RegData_in(MEM_RegData),
    .CLK(CLK), .IR_out(WB_IR), .PC_out(WB_PC), .RS1_out(WB_RS1), .RS2_out_2(WB_RS2), .RegData_out(RDin),
    .halt(halt), .RegWrite_in(MEM_RegWrite), .RegWrite_out(RegWrite), .RegWriteNum_in(MEM_RegWriteNum),
    .RegWriteNum_out(WB_RegWriteNum), .ecall_in(ex_mem_1_ecall_out), .ecall_out(WB_ecall));  // open: MemData_in, MemData_out, MemWrite_in, MemWrite_out, MemWriteAddr_in, MemWriteAddr_out
  Comparator #(.width(32), .mode("twosComplement")) comparator_3 (
    .a(WB_RS1), .b(32'h22), .eq(comparator_3_eq));  // open: gt, lt
  not not_5 (not_5_out, comparator_3_eq);
  and and_6 (and_6_out, comparator_3_eq, WB_ecall);
  and and_7 (and_7_out, not_5_out, WB_ecall);
  Register #(.width(1), .trigger("falling"), .Select("low")) register_1 (
    .D(1'b1), .en(and_7_out), .Q(halt), .clk(CLK), .clr(Go));
  Register #(.width(32), .trigger("rising"), .Select("low")) register_2 (
    .D(WB_RS2), .en(and_6_out), .Q(LedData), .clk(CLK));  // open: clr

  // Other names for the same wires on the sheet: MEM_MemData[31:0] = MDin; MEM_MemWrite = MemWrite;
  //   MEM_PC[31:0] = M_PC; WB_RegData[31:0] = RDin; WB_RegWrite = RegWrite

  // Notes on the sheet:
  //   中断源
  //   时空图监测，可删除
  //   中断等待指示
  //   指令存储器
  //   数码管输出
  //   contents of rom_1 (hex, n*v repeats v):
  //   100493 100006f 100493 200913 300993 100006f 100493 200913 300993 100006f 100493 200913 300993
  //   100006f 100493 200913 300993 29c000ef 100413 100493 1f49493 900533 2200893 73 24d493 48463 fedff06f
  //   900533 2200893 73 100493 249493 900533 2200893 73 48463 fedff06f 100493 1f49493 900533 2200893 73
  //   4034d493 900533 2200893 73 4044d493 900533 2200893 73 4044d493 900533 2200893 73 4044d493 900533
  //   2200893 73 4044d493 900533 2200893 73 4044d493 900533 2200893 73 4044d493 900533 2200893 73 4044d493
  //   900533 2200893 73 100413 1f41993 41f9d993 433 c00913 300b13 140413 f47413 800293 100313 499993
  //   89e9b3 1300533 2200893 73 406282b3 fe0294e3 140413 f00f93 1f47433 1c41413 800293 100313 49d993
  //   89e9b3 1300533 2200893 73 406282b3 fe0294e3 1c45413 406b0b33 b0463 f95ff06f 2b3 fff2c293 829293
  //   ff2e293 500533 2200893 73 fff00413 493 84a023 140413 448493 84a023 140413 448493 84a023 140413
  //   448493 84a023 140413 448493 84a023 140413 448493 84a023 140413 448493 84a023 140413 448493 84a023
  //   140413 448493 84a023 140413 448493 84a023 140413 448493 84a023 140413 448493 84a023 140413 448493
  //   84a023 140413 448493 84a023 140413 448493 84a023 140413 448493 84a023 140413 448493 140413 433
  //   3c00493 42983 4aa03 149a2b3 28663 134a023 1442023 ffc48493 fe9412e3 800533 2200893 73 440413 3c00493
  //   fc9416e3 a00893 73 413 140413 800533 2200893 73 240413 800533 2200893 73 340413 800533 2200893 73
  //   440413 800533 2200893 73 540413 800533 2200893 73 640413 800533 2200893 73 740413 800533 2200893 73
  //   840413 800533 2200893 2200893 73 8067
  //   continue or jump
  //   URET
  //   I
  //   S
  //   shamt
  //   B
  //   U
  //   J
  //   控制位
  //   流水调试日志用
  //   暂停节拍，不能为0
  //   戳工具置1进入计数暂停模式，ctrl+k时钟自动运行到对应节拍暂停
  //   ctrl+k关闭时钟连续运行，将控制位置零，进入单步调试模式调试
  //   可计数暂停的时钟源
  //   j or b
  //   jal or jalr
  //   为方便自动评测，需要输出流水线各段保存的PC值，注意是PC不是PC+4，另外ID段寄存器写入信息，Mem段内存写入信息也要输出
  //   AluSrcB
  //   data or RA
  //   数据存储器
  //   from alu or mem
endmodule

module \EX重定向逻辑  (
  input  BranchTaken,
  input  EX_RegWrite,
  input  [4:0] EX_RegWriteNum,
  input  MEM_RegWrite,
  input  [4:0] MEM_RegWriteNum,
  input  EX_Mem2Reg,
  input  [31:0] ID_IR,
  output [1:0] R1_fwd,
  output Flush,
  output [1:0] R2_fwd,
  output LoadUse
);

  wire and_3_out, and_5_out, comparator_1_eq, comparator_2_eq, comparator_3_eq, comparator_4_eq,
       comparator_5_eq, comparator_6_eq, comparator_7_eq, comparator_8_eq, comparator_9_eq, comparator_10_eq,
       comparator_11_eq, comparator_12_eq, comparator_13_eq, comparator_14_eq, comparator_15_eq,
       comparator_16_eq, comparator_17_eq, ecall, not_1_out, not_2_out, not_3_out, not_4_out, or_3_out,
       R1_EX_Hazzard, R1use, R2_EX_Hazzard, R2use;
  wire [4:0] R1, R2;

  Comparator #(.width(5), .mode("twosComplement")) comparator_1 (
    .a(5'b00100), .b(ID_IR[6:2]), .eq(comparator_1_eq));  // open: gt, lt
  Comparator #(.width(5), .mode("twosComplement")) comparator_2 (
    .a(5'b01000), .b(ID_IR[6:2]), .eq(comparator_2_eq));  // open: gt, lt
  Comparator #(.width(5), .mode("twosComplement")) comparator_3 (
    .a(5'b11000), .b(ID_IR[6:2]), .eq(comparator_3_eq));  // open: gt, lt
  Comparator #(.width(5), .mode("twosComplement")) comparator_4 (
    .a(5'b00011), .b(ID_IR[6:2]), .eq(comparator_4_eq));  // open: gt, lt
  Comparator #(.width(5), .mode("twosComplement")) comparator_5 (
    .a(5'b11001), .b(ID_IR[6:2]), .eq(comparator_5_eq));  // open: gt, lt
  Comparator #(.width(5), .mode("twosComplement")) comparator_6 (
    .a({5{1'b0}}), .b(ID_IR[6:2]), .eq(comparator_6_eq));  // open: gt, lt
  Comparator #(.width(5), .mode("twosComplement")) comparator_7 (
    .a(5'b01100), .b(ID_IR[6:2]), .eq(comparator_7_eq));  // open: gt, lt
  Multiplexer #(.select(1), .width(5), .disabled("Z"), .enable("false")) multiplexer_1 (
    .in0(ID_IR[19:15]), .in1(5'b10001), .out(R1), .sel(ecall));
  Multiplexer #(.select(1), .width(5), .disabled("Z"), .enable("false")) multiplexer_2 (
    .in0(ID_IR[24:20]), .in1(5'b01010), .out(R2), .sel(ecall));
  Comparator #(.width(5), .mode("twosComplement")) comparator_8 (
    .a(ID_IR[6:2]), .b(5'b11100), .eq(comparator_8_eq));  // open: gt, lt
  Comparator #(.width(12), .mode("twosComplement")) comparator_9 (
    .a(ID_IR[31:20]), .b({12{1'b0}}), .eq(comparator_9_eq));  // open: gt, lt
  or or_1 (R1use, comparator_1_eq, comparator_2_eq, comparator_4_eq, comparator_5_eq, comparator_6_eq, comparator_7_eq, comparator_3_eq, ecall);
  or or_2 (R2use, comparator_7_eq, comparator_3_eq, comparator_2_eq, ecall);
  and and_1 (ecall, comparator_8_eq, comparator_9_eq);
  Comparator #(.width(5), .mode("twosComplement")) comparator_10 (
    .a(R1), .b({5{1'b0}}), .eq(comparator_10_eq));  // open: gt, lt
  not not_1 (not_1_out, comparator_10_eq);
  Comparator #(.width(5), .mode("twosComplement")) comparator_11 (
    .a(R1), .b(EX_RegWriteNum), .eq(comparator_11_eq));  // open: gt, lt
  Comparator #(.width(5), .mode("twosComplement")) comparator_12 (
    .a(R1), .b({5{1'b0}}), .eq(comparator_12_eq));  // open: gt, lt
  not not_2 (not_2_out, comparator_12_eq);
  Comparator #(.width(5), .mode("twosComplement")) comparator_13 (
    .a(R1), .b(MEM_RegWriteNum), .eq(comparator_13_eq));  // open: gt, lt
  Comparator #(.width(5), .mode("twosComplement")) comparator_14 (
    .a(R2), .b({5{1'b0}}), .eq(comparator_14_eq));  // open: gt, lt
  not not_3 (not_3_out, comparator_14_eq);
  Comparator #(.width(5), .mode("twosComplement")) comparator_15 (
    .a(R2), .b(EX_RegWriteNum), .eq(comparator_15_eq));  // open: gt, lt
  not not_4 (not_4_out, comparator_16_eq);
  Comparator #(.width(5), .mode("twosComplement")) comparator_16 (
    .a(R2), .b({5{1'b0}}), .eq(comparator_16_eq));  // open: gt, lt
  Comparator #(.width(5), .mode("twosComplement")) comparator_17 (
    .a(R2), .b(MEM_RegWriteNum), .eq(comparator_17_eq));  // open: gt, lt
  and and_2 (R1_EX_Hazzard, R1use, not_1_out, comparator_11_eq, EX_RegWrite);
  and and_3 (and_3_out, R1use, not_2_out, comparator_13_eq, MEM_RegWrite);
  and and_4 (R2_EX_Hazzard, R2use, not_3_out, comparator_15_eq, EX_RegWrite);
  and and_5 (and_5_out, R2use, not_4_out, comparator_17_eq, MEM_RegWrite);
  or or_3 (or_3_out, R1_EX_Hazzard, R2_EX_Hazzard);
  and and_6 (LoadUse, EX_Mem2Reg, or_3_out);
  Priority_Encoder #(.select(2), .disabled("Z")) priority_encoder_1 (
    .in0(1'b1), .in1(and_3_out), .in2(R1_EX_Hazzard), .out(R1_fwd));  // open: in3, gs, en_out, en_in
  Priority_Encoder #(.select(2), .disabled("Z")) priority_encoder_2 (
    .in0(1'b1), .in1(and_5_out), .in2(R2_EX_Hazzard), .out(R2_fwd));  // open: in3, gs, en_out, en_in

  assign Flush = BranchTaken;
endmodule

module \气泡流水线  (
  output RegWrite,
  output MemWrite,
  output [31:0] IF_PC,
  output [31:0] ID_PC,
  output [31:0] EX_PC,
  output [31:0] M_PC,
  output [31:0] WB_PC,
  output [31:0] RDin,
  output [31:0] MDin,
  output [31:0] LedData
);

  wire alu_1_equal, and_1_out, and_2_out, and_3_out, and_4_out, and_5_out, and_6_out, and_7_out, BranchTaken,
       CLK, clock_1_out, comparator_1_eq, comparator_1_lt, comparator_2_eq, comparator_2_gt, comparator_3_eq,
       d_ff_1_q, EX_ALU_src, EX_beq, EX_bge, EX_BJump, EX_bne, EX_jal, EX_jalr, EX_JJump, ex_mem_1_ecall_out,
       EX_RegWrite, \ex气泡逻辑_1_flush , \ex气泡逻辑_1_stall , Go, halt, ID_ALU_src, ID_beq, ID_bge, ID_bne,
       ID_ecall, id_ex_1_ecall_out, id_ex_1_lui_out, id_ex_1_mem2reg_out, id_ex_1_memwrite_out,
       id_ex_1_sh_out, ID_jal, ID_jalr, ID_lui, ID_Mem2Reg, ID_MemWrite, ID_RegWrite, ID_sh, IR1, IR2, IR3,
       MEM_lui, MEM_Mem2Reg, MEM_NeedLink, MEM_RegWrite, MEM_sh, nand_1_out, not_1_out, not_2_out, not_3_out,
       not_4_out, not_5_out, or_2_out, or_3_out, RST, S, ShiftImm, W1, W2, W3, WB_ecall, \单周期硬布线控制器_1_uret ;
  wire [3:0] EX_ALU_op, ID_ALU_op;
  wire [4:0] EX_RegWriteNum, MEM_RegWriteNum, multiplexer_2_out, multiplexer_3_out, WB_RegWriteNum;
  wire [11:0] multiplexer_4_out;
  wire [12:0] CNT_num;
  wire [15:0] \LoadUse次数 , ram_1_data, \总周期数 , \插入气泡数 , \无条件分支数 , \条件分支成功数 ;
  wire [31:0] adder_2_out, adder_3_out, adder_4_out, bit_extender_1_out, bit_extender_2_out,
       bit_extender_3_out, bit_extender_4_out, bit_extender_5_out, EX_ALU_res, EX_BImm, EX_IR, EX_ISImm,
       EX_JImm, ex_mem_1_rs1_out, EX_RS1, EX_RS2, id_ex_1_uimm_out, ID_IR, IF_IR, IF_PC_4, MEM_ALU_res,
       MEM_IR, MEM_RegData, MEM_RS2, MEM_UImm, multiplexer_1_out, multiplexer_5_out, multiplexer_6_out,
       multiplexer_7_out, multiplexer_8_out, multiplexer_11_out, multiplexer_12_out, multiplexer_13_out,
       regfileforbubble_1_r1, regfileforbubble_1_r2, shifter_1_out, shifter_2_out, shifter_3_out, WB_IR,
       WB_RS1, WB_RS2;
  wire [31:16] ram_1_data_2;

  Button \u_总复位  (.out(RST));
  Button _1 (.out(IR1));
  Button _2 (.out(IR2));
  Button _3 (.out(IR3));
  // Probe on \总周期数 
  // Probe on \总周期数 
  not not_1 (not_1_out, halt);
  and and_1 (and_1_out, not_1_out, not_2_out);
  Register #(.width(32), .trigger("rising"), .Select("low")) PC (
    .D(multiplexer_1_out), .en(and_1_out), .Q(IF_PC), .clk(CLK), .clr(RST));
  Button \u_继续运行  (.out(Go));
  LED #(.active("true")) led_1 (.in(W1));
  LED #(.active("true")) led_2 (.in(W2));
  LED #(.active("true")) led_3 (.in(W3));
  not not_2 (not_2_out, \ex气泡逻辑_1_stall );
  Hex_Digit_Display hex_digit_display_1 (.value(LedData[31:28]));  // open: dp
  // Probe on IF_PC[19:0]
  // RiscV_Probe riscv_probe_1: pin names not known; wires that end beside it: IF_IR
  Counter #(.width(16), .max('hffff), .ongoal("wrap"), .trigger("rising"), .behavior("new")) counter_1 (
    .Q(\总周期数 ), .clk(CLK));  // open: load, D, count, carry, clr, preset, down
  Counter #(.width(16), .max('hffff), .ongoal("wrap"), .trigger("rising"), .behavior("new")) counter_2 (
    .Q(\无条件分支数 ), .clk(EX_JJump));  // open: load, D, count, carry, clr, preset, down
  Adder #(.width(32)) adder_1 (.a(32'h4), .b(IF_PC), .out(IF_PC_4), .cin(1'b0));  // open: cout
  Hex_Digit_Display hex_digit_display_2 (.value(LedData[27:24]));  // open: dp
  Hex_Digit_Display hex_digit_display_3 (.value(LedData[23:20]));  // open: dp
  // Probe on ID_PC[19:0]
  // RiscV_Probe riscv_probe_2: pin names not known; wires that end beside it: ID_IR
  and and_2 (and_2_out, not_3_out, \ex气泡逻辑_1_flush );
  not not_3 (not_3_out, BranchTaken);
  Hex_Digit_Display hex_digit_display_4 (.value(LedData[19:16]));  // open: dp
  Hex_Digit_Display hex_digit_display_5 (.value(LedData[15:12]));  // open: dp
  Counter #(.width(16), .max('hffff), .ongoal("wrap"), .trigger("rising"), .behavior("new")) counter_3 (
    .Q(\条件分支成功数 ), .clk(EX_BJump));  // open: load, D, count, carry, clr, preset, down
  Counter #(.width(16), .max('hffff), .ongoal("wrap"), .trigger("falling"), .behavior("new")) counter_4 (
    .count(and_2_out), .Q(\插入气泡数 ), .clk(CLK));  // open: load, D, carry, clr, preset, down
  ROM #(.addrWidth(10), .dataWidth(32), .Select("high")) rom_1 (.addr(IF_PC[11:2]), .data(IF_IR));
  Multiplexer #(.select(1), .width(32), .disabled("Z"), .enable("false")) multiplexer_1 (
    .in0(IF_PC_4), .in1(multiplexer_6_out), .out(multiplexer_1_out), .sel(BranchTaken));
  Hex_Digit_Display hex_digit_display_6 (.value(LedData[7:4]));  // open: dp
  Hex_Digit_Display hex_digit_display_7 (.value(LedData[11:8]));  // open: dp
  // Probe on EX_PC[19:0]
  // RiscV_Probe riscv_probe_3: pin names not known; wires that end beside it: EX_IR
  IF_ID if_id_1 (
    .IRin(IF_IR), .PCin(IF_PC), .CLK(CLK), .IRout(ID_IR), .PCout(ID_PC), .clear(BranchTaken),
    .Stall(\ex气泡逻辑_1_stall ), .halt(halt));
  or or_1 (BranchTaken, EX_JJump, EX_BJump);
  Hex_Digit_Display hex_digit_display_8 (.value(LedData[3:0]));  // open: dp
  // Probe on \总周期数 
  // Probe on M_PC[19:0]
  // RiscV_Probe riscv_probe_4: pin names not known; wires that end beside it: MEM_IR
  // Probe on \总周期数 
  // Probe on \无条件分支数 
  // Probe on \条件分支成功数 
  // Probe on \插入气泡数 
  // Probe on \LoadUse次数 
  \单周期硬布线控制器  \u_单周期硬布线控制器_1  (
    .Funct({ID_IR[30], ID_IR[25], ID_IR[14:12]}), .OP(ID_IR[6:2]), .ALU_OP(ID_ALU_op), .MemToReg(ID_Mem2Reg),
    .MemWrite(ID_MemWrite), .ALU_SRC(ID_ALU_src), .ecall(ID_ecall), .bge(ID_bge), .beq(ID_beq), .lui(ID_lui),
    .S_Type(S), .RegWrite(ID_RegWrite), .in_3(ID_IR[21]), .uret(\单周期硬布线控制器_1_uret ), .ShitfImm(ShiftImm),
    .bne(ID_bne), .jalr(ID_jalr), .jal(ID_jal), .sh(ID_sh));  // open: B_Type
  Multiplexer #(.select(1), .width(5), .disabled("Z"), .enable("false")) multiplexer_2 (
    .in0(ID_IR[19:15]), .in1(5'b10001), .out(multiplexer_2_out), .sel(ID_ecall));
  Multiplexer #(.select(1), .width(5), .disabled("Z"), .enable("false")) multiplexer_3 (
    .in0(ID_IR[24:20]), .in1(5'b01010), .out(multiplexer_3_out), .sel(ID_ecall));
  assign bit_extender_1_out = {{27{ID_IR[24]}}, ID_IR[24:20]};  // Bit_Extender bit_extender_1
  assign bit_extender_2_out = {{12{1'b0}}, ID_IR[31:12]};  // Bit_Extender bit_extender_2
  // Probe on IF_PC[11:0]
  // Probe on WB_PC[19:0]
  // RiscV_Probe riscv_probe_5: pin names not known; wires that end beside it: WB_IR
  Multiplexer #(.select(1), .width(12), .disabled("Z"), .enable("false")) multiplexer_4 (
    .in0(ID_IR[31:20]), .in1({ID_IR[31:25], ID_IR[11:7]}), .out(multiplexer_4_out), .sel(S));
  // Probe on EX_PC[11:0]
  // Probe on ID_PC[11:0]
  assign bit_extender_3_out = {{20{multiplexer_4_out[11]}}, multiplexer_4_out};  // Bit_Extender bit_extender_3
  Multiplexer #(.select(1), .width(32), .disabled("Z"), .enable("false")) multiplexer_5 (
    .in0(bit_extender_3_out), .in1(bit_extender_1_out), .out(multiplexer_5_out), .sel(ShiftImm));
  assign bit_extender_4_out = {{20{ID_IR[31]}}, {ID_IR[31], ID_IR[7], ID_IR[30:25], ID_IR[11:8]}};  // Bit_Extender bit_extender_4
  Shifter #(.width(32), .shift("ll")) shifter_1 (.in(bit_extender_2_out), .\dist (5'b01100), .out(shifter_1_out));
  assign bit_extender_5_out = {{12{ID_IR[31]}}, {ID_IR[31], ID_IR[19:12], ID_IR[20], ID_IR[30:21]}};  // Bit_Extender bit_extender_5
  // Probe on M_PC[11:0]
  D_Flip_Flop #(.trigger("high"), .Pre_Clr_Positions("LEGACY"), .NegatePresetClear("false"), .enable("true"), .NewFFLayout("false")) d_ff_1 (.Q(d_ff_1_q));  // open: clk, D, Qn, preset, en, reset
  // Probe on 13'h11b
  RegFileForBubble regfileforbubble_1 (
    .Din(RDin), .Clk(CLK), .R1(regfileforbubble_1_r1), .R2(regfileforbubble_1_r2), .WE(RegWrite),
    .W_num(WB_RegWriteNum), .R1_num(multiplexer_2_out), .R2_num(multiplexer_3_out));
  // Probe on WB_PC[11:0]
  Comparator #(.width(13), .mode("twosComplement")) comparator_1 (
    .a(CNT_num), .b(13'h11b), .eq(comparator_1_eq), .lt(comparator_1_lt));  // open: gt
  Clock #(.highDuration(1), .lowDuration(1)) clock_1 (.out(clock_1_out));
  nand nand_1 (nand_1_out, d_ff_1_q, comparator_1_eq);
  Counter #(.width(13), .max('h1fff), .ongoal("stay"), .trigger("rising"), .behavior("old")) counter_5 (
    .count(comparator_1_lt), .Q(CNT_num), .clk(clock_1_out));  // open: load, D, carry, clr, preset
  assign CLK = nand_1_out ? clock_1_out : 1'bz;  // Controlled_Buffer controlled_buffer_1
  Pull_Resistor #(.pull(1)) pull_resistor_1 (.node(CLK));
  Multiplexer #(.select(1), .width(32), .disabled("Z"), .enable("false")) multiplexer_6 (
    .in0(multiplexer_7_out), .in1(adder_2_out), .out(multiplexer_6_out), .sel(or_2_out));
  or or_2 (or_2_out, EX_bne, EX_beq, EX_bge);
  ID_EX id_ex_1 (
    .IRin(ID_IR), .IRout(EX_IR), .PCout(EX_PC), .RS1out(EX_RS1), .RS2out(EX_RS2), .Imm_out(EX_ISImm),
    .RegWrite_out(EX_RegWrite), .MemWrite_out(id_ex_1_memwrite_out), .RegWriteNum_out(EX_RegWriteNum),
    .ALU_src_out(EX_ALU_src), .jal_out(EX_jal), .jalr_out(EX_jalr), .beq_out(EX_beq), .bne_out(EX_bne),
    .bge_out(EX_bge), .sh_out(id_ex_1_sh_out), .CLK(CLK), .lui_out(id_ex_1_lui_out),
    .ecall_out(id_ex_1_ecall_out), .Mem2Reg_out(id_ex_1_mem2reg_out), .BImm_out(EX_BImm),
    .UImm_out(id_ex_1_uimm_out), .JImm_out(EX_JImm), .ALU_op_out(EX_ALU_op), .PCin(ID_PC),
    .RS1in(regfileforbubble_1_r1), .RS2in(regfileforbubble_1_r2), .Imm_in(multiplexer_5_out),
    .RegWrite_in(ID_RegWrite), .MemWrite_in(ID_MemWrite), .RegWriteNum_in(ID_IR[11:7]),
    .ALU_src_in(ID_ALU_src), .jal_in(ID_jal), .jalr_in(ID_jalr), .beq_in(ID_beq), .bne_in(ID_bne),
    .bge_in(ID_bge), .sh_in(ID_sh), .lui_in(ID_lui), .ecall_in(ID_ecall), .Mem2Reg_in(ID_Mem2Reg),
    .BImm_in(bit_extender_4_out), .UImm_in(shifter_1_out), .JImm_in(bit_extender_5_out),
    .ALI_op_in(ID_ALU_op), .clear(\ex气泡逻辑_1_flush ), .halt(halt));
  Multiplexer #(.select(1), .width(32), .disabled("Z"), .enable("false")) multiplexer_7 (
    .in0(adder_3_out), .in1(EX_ALU_res), .out(multiplexer_7_out), .sel(EX_jalr));
  Shifter #(.width(32), .shift("ll")) shifter_2 (.in(EX_BImm), .\dist (5'b00001), .out(shifter_2_out));
  Shifter #(.width(32), .shift("ll")) shifter_3 (.in(EX_JImm), .\dist (5'b00001), .out(shifter_3_out));
  Adder #(.width(32)) adder_2 (.a(shifter_2_out), .b(EX_PC), .out(adder_2_out), .cin(1'b0));  // open: cout
  Adder #(.width(32)) adder_3 (.a(shifter_3_out), .b(EX_PC), .out(adder_3_out), .cin(1'b0));  // open: cout
  Multiplexer #(.select(1), .width(32), .disabled("Z"), .enable("false")) multiplexer_8 (
    .in0(EX_RS2), .in1(EX_ISImm), .out(multiplexer_8_out), .sel(EX_ALU_src));
  \EX气泡逻辑  \ex气泡逻辑_1  (
    .BranchTaken(BranchTaken), .EX_RegWrite(EX_RegWrite), .EX_RegWriteNum(EX_RegWriteNum),
    .MEM_RegWrite(MEM_RegWrite), .MEM_RegWriteNum(MEM_RegWriteNum), .ID_IR(ID_IR), .Stall(\ex气泡逻辑_1_stall ),
    .Flush(\ex气泡逻辑_1_flush ));
  not not_4 (not_4_out, alu_1_equal);
  and and_3 (and_3_out, not_4_out, EX_bne);
  Comparator #(.width(32), .mode("twosComplement")) comparator_2 (
    .a(EX_RS1), .b(EX_RS2), .gt(comparator_2_gt), .eq(comparator_2_eq));  // open: lt
  ALU alu_1 (
    .X(EX_RS1), .Y(multiplexer_8_out), .AluOP(EX_ALU_op), .Equal(alu_1_equal), .Result(EX_ALU_res));  // open: Result_2, out_4, out_6
  and and_4 (and_4_out, alu_1_equal, EX_beq);
  or or_3 (or_3_out, comparator_2_gt, comparator_2_eq);
  or or_4 (EX_JJump, EX_jal, EX_jalr);
  or or_5 (EX_BJump, and_4_out, and_3_out, and_5_out);
  and and_5 (and_5_out, EX_bge, or_3_out);
  EX_MEM ex_mem_1 (
    .IR_in(EX_IR), .PC_in(EX_PC), .RS1_in(EX_RS1), .RS2_in(EX_RS2), .UImm_in(id_ex_1_uimm_out),
    .ALU_result_in(EX_ALU_res), .NeedLink_in(EX_JJump), .RegWrite_in(EX_RegWrite),
    .MemWrite_in(id_ex_1_memwrite_out), .RegWriteNum_in(EX_RegWriteNum), .lui_in(id_ex_1_lui_out),
    .ecall_in(id_ex_1_ecall_out), .sh_in(id_ex_1_sh_out), .Mem2Reg_in(id_ex_1_mem2reg_out), .CLK(CLK),
    .IR_out(MEM_IR), .PC_out(M_PC), .RS1_out(ex_mem_1_rs1_out), .RS2_out(MEM_RS2), .UImm_out(MEM_UImm),
    .ALU_result_out(MEM_ALU_res), .NeedLink_out(MEM_NeedLink), .RegWrite_out(MEM_RegWrite),
    .MemWrite_out(MemWrite), .RegWriteNum_out(MEM_RegWriteNum), .lui_out(MEM_lui),
    .ecall_out(ex_mem_1_ecall_out), .sh_out(MEM_sh), .Mem2Reg_out(MEM_Mem2Reg), .halt(halt));
  Multiplexer #(.select(1), .width(32), .disabled("Z"), .enable("false")) multiplexer_9 (
    .in0(MEM_RS2), .in1(multiplexer_11_out), .out(MDin), .sel(MEM_sh));
  Multiplexer #(.select(1), .width(32), .disabled("Z"), .enable("false")) multiplexer_10 (
    .in0(multiplexer_13_out), .in1(adder_4_out), .out(MEM_RegData), .sel(MEM_NeedLink));
  Adder #(.width(32)) adder_4 (.a(32'h4), .b(M_PC), .out(adder_4_out));  // open: cin, cout
  RAM #(.addrWidth(10), .dataWidth(32), .bus("separate"), .Select("high")) ram_1 (
    .addr(MEM_ALU_res[11:2]), .din(MDin), .data({ram_1_data_2, ram_1_data}), .str(MemWrite), .clk(CLK));  // open: sel, ld, clr
  Multiplexer #(.select(1), .width(32), .disabled("Z"), .enable("false")) multiplexer_11 (
    .in0({ram_1_data_2, MEM_RS2[15:0]}), .in1({MEM_RS2[15:0], ram_1_data}), .out(multiplexer_11_out),
    .sel(MEM_ALU_res[1]));
  Multiplexer #(.select(1), .width(32), .disabled("Z"), .enable("false")) multiplexer_12 (
    .in0(MEM_ALU_res), .in1({ram_1_data_2, ram_1_data}), .out(multiplexer_12_out), .sel(MEM_Mem2Reg));
  Multiplexer #(.select(1), .width(32), .disabled("Z"), .enable("false")) multiplexer_13 (
    .in0(multiplexer_12_out), .in1(MEM_UImm), .out(multiplexer_13_out), .sel(MEM_lui));
  MEM_WB mem_wb_1 (
    .IR_in(MEM_IR), .PC_in(M_PC), .RS1_in(ex_mem_1_rs1_out), .RS2_out(MEM_RS2), .RegData_in(MEM_RegData),
    .CLK(CLK), .IR_out(WB_IR), .PC_out(WB_PC), .RS1_out(WB_RS1), .RS2_out_2(WB_RS2), .RegData_out(RDin),
    .halt(halt), .RegWrite_in(MEM_RegWrite), .RegWrite_out(RegWrite), .RegWriteNum_in(MEM_RegWriteNum),
    .RegWriteNum_out(WB_RegWriteNum), .ecall_in(ex_mem_1_ecall_out), .ecall_out(WB_ecall));  // open: MemData_in, MemData_out, MemWrite_in, MemWrite_out, MemWriteAddr_in, MemWriteAddr_out
  Comparator #(.width(32), .mode("twosComplement")) comparator_3 (
    .a(WB_RS1), .b(32'h22), .eq(comparator_3_eq));  // open: gt, lt
  not not_5 (not_5_out, comparator_3_eq);
  and and_6 (and_6_out, comparator_3_eq, WB_ecall);
  and and_7 (and_7_out, not_5_out, WB_ecall);
  Register #(.width(1), .trigger("falling"), .Select("low")) register_1 (
    .D(1'b1), .en(and_7_out), .Q(halt), .clk(CLK), .clr(Go));
  Register #(.width(32), .trigger("rising"), .Select("low")) register_2 (
    .D(WB_RS2), .en(and_6_out), .Q(LedData), .clk(CLK));  // open: clr

  // Other names for the same wires on the sheet: MEM_MemData[31:0] = MDin; MEM_MemWrite = MemWrite;
  //   MEM_PC[31:0] = M_PC; WB_RegData[31:0] = RDin; WB_RegWrite = RegWrite

  // Notes on the sheet:
  //   中断源
  //   时空图监测，可删除
  //   中断等待指示
  //   指令存储器
  //   数码管输出
  //   contents of rom_1 (hex, n*v repeats v):
  //   100493 100006f 100493 200913 300993 100006f 100493 200913 300993 100006f 100493 200913 300993
  //   100006f 100493 200913 300993 3b8000ef 100413 100493 1f49493 900533 2200893 73 24d493 48463 fedff06f
  //   900533 2200893 73 100493 249493 900533 2200893 73 48463 fedff06f 100493 1f49493 900533 2200893 73
  //   4034d493 900533 2200893 73 4044d493 900533 2200893 73 4044d493 900533 2200893 73 4044d493 900533
  //   2200893 73 4044d493 900533 2200893 73 4044d493 900533 2200893 73 4044d493 900533 2200893 73 4044d493
  //   900533 2200893 73 100413 1f41993 41f9d993 433 c00913 300b13 140413 f47413 800293 100313 499993
  //   89e9b3 1300533 2200893 73 406282b3 fe0294e3 140413 f00f93 1f47433 1c41413 800293 100313 49d993
  //   89e9b3 1300533 2200893 73 406282b3 fe0294e3 1c45413 406b0b33 b0463 f95ff06f 2b3 fff2c293 829293
  //   ff2e293 500533 2200893 73 fff00413 493 84a023 140413 448493 84a023 140413 448493 84a023 140413
  //   448493 84a023 140413 448493 84a023 140413 448493 84a023 140413 448493 84a023 140413 448493 84a023
  //   140413 448493 84a023 140413 448493 84a023 140413 448493 84a023 140413 448493 84a023 140413 448493
  //   84a023 140413 448493 84a023 140413 448493 84a023 140413 448493 84a023 140413 448493 140413 433
  //   3c00493 42983 4aa03 149a2b3 28663 134a023 1442023 ffc48493 fe9412e3 800533 2200893 73 440413 3c00493
  //   fc9416e3 100293 300313 800493 849493 7648493 1449493 900533 2200893 73 800e13 4054d4b3 4064d4b3
  //   900533 2200893 73 fffe0e13 fe0e14e3 a00893 73 800e13 fedc04b7 fff00413 1045413 84e4b3 900533 2200893
  //   73 ba984b7 900533 73 76544b7 900533 73 32104b7 900533 73 fffe0e13 fa0e1ee3 a00893 73 313 2000e13
  //   100493 100913 931023 900533 2200893 73 12484b3 230313 fffe0e13 fe0e12e3 1000e13 313 32483 900533
  //   2200893 73 430313 fffe0e13 fe0e14e3 a00893 73 f00493 900533 2200893 73 fff48493 fe04d8e3 a00893 73
  //   a00893 73 413 140413 800533 2200893 73 240413 800533 2200893 73 340413 800533 2200893 73 440413
  //   800533 2200893 73 540413 800533 2200893 73 640413 800533 2200893 73 740413 800533 2200893 73 840413
  //   800533 2200893 2200893 73 8067
  //   continue or jump
  //   URET
  //   I
  //   S
  //   shamt
  //   B
  //   U
  //   J
  //   控制位
  //   流水调试日志用
  //   暂停节拍，不能为0
  //   戳工具置1进入计数暂停模式，ctrl+k时钟自动运行到对应节拍暂停
  //   ctrl+k关闭时钟连续运行，将控制位置零，进入单步调试模式调试
  //   可计数暂停的时钟源
  //   j or b
  //   jal or jalr
  //   为方便自动评测，需要输出流水线各段保存的PC值，注意是PC不是PC+4，另外ID段寄存器写入信息，Mem段内存写入信息也要输出
  //   AluSrcB
  //   data or RA
  //   数据存储器
  //   from alu or mem
endmodule

module \EX气泡逻辑  (
  input  BranchTaken,
  input  EX_RegWrite,
  input  [4:0] EX_RegWriteNum,
  input  MEM_RegWrite,
  input  [4:0] MEM_RegWriteNum,
  input  [31:0] ID_IR,
  output Stall,
  output Flush
);

  wire and_2_out, and_3_out, and_4_out, and_5_out, comparator_1_eq, comparator_2_eq, comparator_3_eq,
       comparator_4_eq, comparator_5_eq, comparator_6_eq, comparator_7_eq, comparator_8_eq, comparator_9_eq,
       comparator_10_eq, comparator_11_eq, comparator_12_eq, comparator_13_eq, comparator_14_eq,
       comparator_15_eq, comparator_16_eq, comparator_17_eq, ecall, not_1_out, not_2_out, not_3_out,
       not_4_out, R1use, R2use;
  wire [4:0] R1, R2;

  Comparator #(.width(5), .mode("twosComplement")) comparator_1 (
    .a(5'b00100), .b(ID_IR[6:2]), .eq(comparator_1_eq));  // open: gt, lt
  Comparator #(.width(5), .mode("twosComplement")) comparator_2 (
    .a(5'b01000), .b(ID_IR[6:2]), .eq(comparator_2_eq));  // open: gt, lt
  Comparator #(.width(5), .mode("twosComplement")) comparator_3 (
    .a(5'b11000), .b(ID_IR[6:2]), .eq(comparator_3_eq));  // open: gt, lt
  Comparator #(.width(5), .mode("twosComplement")) comparator_4 (
    .a(5'b00011), .b(ID_IR[6:2]), .eq(comparator_4_eq));  // open: gt, lt
  Comparator #(.width(5), .mode("twosComplement")) comparator_5 (
    .a(5'b11001), .b(ID_IR[6:2]), .eq(comparator_5_eq));  // open: gt, lt
  Comparator #(.width(5), .mode("twosComplement")) comparator_6 (
    .a({5{1'b0}}), .b(ID_IR[6:2]), .eq(comparator_6_eq));  // open: gt, lt
  Comparator #(.width(5), .mode("twosComplement")) comparator_7 (
    .a(5'b01100), .b(ID_IR[6:2]), .eq(comparator_7_eq));  // open: gt, lt
  Multiplexer #(.select(1), .width(5), .disabled("Z"), .enable("false")) multiplexer_1 (
    .in0(ID_IR[19:15]), .in1(5'b10001), .out(R1), .sel(ecall));
  Multiplexer #(.select(1), .width(5), .disabled("Z"), .enable("false")) multiplexer_2 (
    .in0(ID_IR[24:20]), .in1(5'b01010), .out(R2), .sel(ecall));
  Comparator #(.width(5), .mode("twosComplement")) comparator_8 (
    .a(ID_IR[6:2]), .b(5'b11100), .eq(comparator_8_eq));  // open: gt, lt
  Comparator #(.width(12), .mode("twosComplement")) comparator_9 (
    .a(ID_IR[31:20]), .b({12{1'b0}}), .eq(comparator_9_eq));  // open: gt, lt
  or or_1 (R1use, comparator_1_eq, comparator_2_eq, comparator_4_eq, comparator_5_eq, comparator_6_eq, comparator_7_eq, comparator_3_eq, ecall);
  or or_2 (R2use, comparator_7_eq, comparator_3_eq, comparator_2_eq, ecall);
  and and_1 (ecall, comparator_8_eq, comparator_9_eq);
  not not_1 (not_1_out, comparator_10_eq);
  Comparator #(.width(5), .mode("twosComplement")) comparator_10 (
    .a(R1), .b({5{1'b0}}), .eq(comparator_10_eq));  // open: gt, lt
  Comparator #(.width(5), .mode("twosComplement")) comparator_11 (
    .a(R1), .b(EX_RegWriteNum), .eq(comparator_11_eq));  // open: gt, lt
  not not_2 (not_2_out, comparator_12_eq);
  Comparator #(.width(5), .mode("twosComplement")) comparator_12 (
    .a(R1), .b({5{1'b0}}), .eq(comparator_12_eq));  // open: gt, lt
  Comparator #(.width(5), .mode("twosComplement")) comparator_13 (
    .a(R1), .b(MEM_RegWriteNum), .eq(comparator_13_eq));  // open: gt, lt
  not not_3 (not_3_out, comparator_14_eq);
  Comparator #(.width(5), .mode("twosComplement")) comparator_14 (
    .a(R2), .b({5{1'b0}}), .eq(comparator_14_eq));  // open: gt, lt
  Comparator #(.width(5), .mode("twosComplement")) comparator_15 (
    .a(R2), .b(EX_RegWriteNum), .eq(comparator_15_eq));  // open: gt, lt
  Comparator #(.width(5), .mode("twosComplement")) comparator_16 (
    .a(R2), .b({5{1'b0}}), .eq(comparator_16_eq));  // open: gt, lt
  not not_4 (not_4_out, comparator_16_eq);
  Comparator #(.width(5), .mode("twosComplement")) comparator_17 (
    .a(R2), .b(MEM_RegWriteNum), .eq(comparator_17_eq));  // open: gt, lt
  and and_2 (and_2_out, R1use, not_1_out, comparator_11_eq, EX_RegWrite);
  and and_3 (and_3_out, R1use, not_2_out, comparator_13_eq, MEM_RegWrite);
  and and_4 (and_4_out, R2use, not_3_out, comparator_15_eq, EX_RegWrite);
  and and_5 (and_5_out, R2use, not_4_out, comparator_17_eq, MEM_RegWrite);
  or or_3 (Stall, and_2_out, and_3_out, and_4_out, and_5_out);
  or or_4 (Flush, Stall, BranchTaken);
endmodule

module RegFileForBubble (
  input  [31:0] Din,
  input  Clk,
  input  WE,
  input  [4:0] R1_num,
  input  [4:0] W_num,
  input  [4:0] R2_num,
  output [31:0] R1,
  output [31:0] R2
);

  // RegisterFile registerfile_1: pin names not known; wires that end beside it: Din, Clk, WE, W_num, R1_num, R2_num, R1, R2
endmodule

module \单周期RISC_V  (
  input  IR1,
  input  IR2,
  input  IR3,
  output RegWrite,
  output MemWrite,
  output [31:0] PC,
  output [31:0] IR,
  output [31:0] RDin,
  output [31:0] MDin,
  output [31:0] LedData
);

  wire alu_1_equal, and_1_out, and_2_out, and_3_out, and_4_out, and_5_out, B, beq, bge, BJump, bne, CLK,
       clock_1_out, comparator_1_eq, comparator_1_gt, comparator_2_eq, comparator_3_eq, comparator_3_lt,
       d_ff_1_q, ecall, Go, halt, IR1_t, IR2_t, IR3_t, IRA, IRB, IRC, jalr, JJump, lui, nand_1_out,
       not_1_out, not_2_out, not_3_out, or_2_out, or_6_out, riscv_probe_1_p2, RST, S, sh, ShiftImm, W1, W2,
       W3, \单周期硬布线控制器_1_alu_src , \单周期硬布线控制器_1_jal , \单周期硬布线控制器_1_memtoreg ;
  wire [3:0] \单周期硬布线控制器_1_alu_op ;
  wire [4:0] multiplexer_2_out, multiplexer_3_out;
  wire [9:0] alu_1_result_2;
  wire [11:0] multiplexer_4_out;
  wire [12:0] CNT_num;
  wire [15:0] regifile_1_r2, \总周期数 ;
  wire [31:0] adder_2_out, adder_3_out, alu_1_result, bit_extender_1_out, bit_extender_2_out,
       bit_extender_3_out, bit_extender_4_out, bit_extender_5_out, multiplexer_1_out, multiplexer_5_out,
       multiplexer_6_out, multiplexer_7_out, multiplexer_8_out, multiplexer_10_out, multiplexer_12_out,
       multiplexer_13_out, PC_4, ram_1_data, regifile_1_r1, shifter_1_out, shifter_2_out, shifter_3_out;
  wire [31:16] regifile_1_r2_2;

  Button \u_继续运行  (.out(Go));
  Button _1 (.out(IRA));
  Button _2 (.out(IRB));
  Button _3 (.out(IRC));
  LED #(.active("true")) led_1 (.in(W1));
  LED #(.active("true")) led_2 (.in(W2));
  LED #(.active("true")) led_3 (.in(W3));
  or or_1 (JJump, jalr, \单周期硬布线控制器_1_jal );
  Register #(.width(32), .trigger("rising"), .Select("low")) u_PC (
    .D(multiplexer_1_out), .en(not_1_out), .Q(PC), .clk(CLK), .clr(RST));
  not not_1 (not_1_out, halt);
  Hex_Digit_Display hex_digit_display_1 (.value(LedData[31:28]));  // open: dp
  Hex_Digit_Display hex_digit_display_2 (.value(LedData[27:24]));  // open: dp
  Hex_Digit_Display hex_digit_display_3 (.value(LedData[23:20]));  // open: dp
  Adder #(.width(32)) adder_1 (.a(32'h4), .b(PC), .out(PC_4), .cin(1'b0));  // open: cout
  Hex_Digit_Display hex_digit_display_4 (.value(LedData[19:16]));  // open: dp
  Hex_Digit_Display hex_digit_display_5 (.value(LedData[15:12]));  // open: dp
  // RiscV_Probe riscv_probe_1: pin names not known; wires that end beside it: IR, riscv_probe_1_p2
  Multiplexer #(.select(1), .width(32), .disabled("Z"), .enable("false")) multiplexer_1 (
    .in0(PC_4), .in1(multiplexer_6_out), .out(multiplexer_1_out), .sel(or_2_out));
  Hex_Digit_Display hex_digit_display_6 (.value(LedData[11:8]));  // open: dp
  Hex_Digit_Display hex_digit_display_7 (.value(LedData[7:4]));  // open: dp
  // Probe on \总周期数 
  ROM #(.addrWidth(10), .dataWidth(32), .Select("high")) rom_1 (.addr(PC[11:2]), .data(IR));
  or or_2 (or_2_out, JJump, BJump);
  Hex_Digit_Display hex_digit_display_8 (.value(LedData[3:0]));  // open: dp
  \单周期硬布线控制器  \u_单周期硬布线控制器_1  (
    .Funct({IR[30], IR[25], IR[14:12]}), .OP(IR[6:2]), .ALU_OP(\单周期硬布线控制器_1_alu_op ),
    .MemToReg(\单周期硬布线控制器_1_memtoreg ), .MemWrite(MemWrite), .ALU_SRC(\单周期硬布线控制器_1_alu_src ), .B_Type(B),
    .ecall(ecall), .bge(bge), .beq(beq), .lui(lui), .S_Type(S), .RegWrite(RegWrite), .in_3(IR[21]),
    .uret(riscv_probe_1_p2), .ShitfImm(ShiftImm), .bne(bne), .jalr(jalr), .jal(\单周期硬布线控制器_1_jal ), .sh(sh));
  Multiplexer #(.select(1), .width(5), .disabled("Z"), .enable("false")) multiplexer_2 (
    .in0(IR[19:15]), .in1(5'b10001), .out(multiplexer_2_out), .sel(ecall));
  Multiplexer #(.select(1), .width(5), .disabled("Z"), .enable("false")) multiplexer_3 (
    .in0(IR[24:20]), .in1(5'b01010), .out(multiplexer_3_out), .sel(ecall));
  assign bit_extender_1_out = {{27{IR[24]}}, IR[24:20]};  // Bit_Extender bit_extender_1
  assign bit_extender_2_out = {{12{1'b0}}, IR[31:12]};  // Bit_Extender bit_extender_2
  or or_3 (IR1_t, IR1, IRA);
  Multiplexer #(.select(1), .width(12), .disabled("Z"), .enable("false")) multiplexer_4 (
    .in0(IR[31:20]), .in1({IR[31:25], IR[11:7]}), .out(multiplexer_4_out), .sel(S));
  assign bit_extender_3_out = {{20{multiplexer_4_out[11]}}, multiplexer_4_out};  // Bit_Extender bit_extender_3
  or or_4 (IR2_t, IR2, IRB);
  Regifile regifile_1 (
    .Din(RDin), .Clk(CLK), .R1(regifile_1_r1), .R2({regifile_1_r2_2, regifile_1_r2}), .WE(RegWrite),
    .W_num(IR[11:7]), .R1_num(multiplexer_2_out), .R2_num(multiplexer_3_out));
  Multiplexer #(.select(1), .width(32), .disabled("Z"), .enable("false")) multiplexer_5 (
    .in0(bit_extender_3_out), .in1(bit_extender_1_out), .out(multiplexer_5_out), .sel(ShiftImm));
  assign bit_extender_4_out = {{20{IR[31]}}, {IR[31], IR[7], IR[30:25], IR[11:8]}};  // Bit_Extender bit_extender_4
  Shifter #(.width(32), .shift("ll")) shifter_1 (.in(bit_extender_2_out), .\dist (5'b01100), .out(shifter_1_out));
  assign bit_extender_5_out = {{12{IR[31]}}, {IR[31], IR[19:12], IR[20], IR[30:21]}};  // Bit_Extender bit_extender_5
  Multiplexer #(.select(1), .width(32), .disabled("Z"), .enable("false")) multiplexer_6 (
    .in0(multiplexer_8_out), .in1(adder_2_out), .out(multiplexer_6_out), .sel(B));
  Multiplexer #(.select(1), .width(32), .disabled("Z"), .enable("false")) multiplexer_7 (
    .in0({regifile_1_r2_2, regifile_1_r2}), .in1(multiplexer_5_out), .out(multiplexer_7_out),
    .sel(\单周期硬布线控制器_1_alu_src ));
  or or_5 (IR3_t, IR3, IRC);
  Shifter #(.width(32), .shift("ll")) shifter_2 (.in(bit_extender_4_out), .\dist (5'b00001), .out(shifter_2_out));
  Shifter #(.width(32), .shift("ll")) shifter_3 (.in(bit_extender_5_out), .\dist (5'b00001), .out(shifter_3_out));
  Multiplexer #(.select(1), .width(32), .disabled("Z"), .enable("false")) multiplexer_8 (
    .in0(adder_3_out), .in1(multiplexer_12_out), .out(multiplexer_8_out), .sel(jalr));
  not not_2 (not_2_out, alu_1_equal);
  and and_1 (and_1_out, not_2_out, bne);
  Comparator #(.width(32), .mode("twosComplement")) comparator_1 (
    .a(regifile_1_r1), .b({regifile_1_r2_2, regifile_1_r2}), .gt(comparator_1_gt), .eq(comparator_1_eq));  // open: lt
  ALU alu_1 (
    .X(regifile_1_r1), .Y(multiplexer_7_out), .AluOP(\单周期硬布线控制器_1_alu_op ), .Equal(alu_1_equal),
    .Result({alu_1_result[31:12], alu_1_result_2, alu_1_result[1:0]}));  // open: Result_2, out_4, out_6
  Multiplexer #(.select(1), .width(32), .disabled("Z"), .enable("false")) multiplexer_9 (
    .in0({regifile_1_r2_2, regifile_1_r2}), .in1(multiplexer_10_out), .out(MDin), .sel(sh));
  Multiplexer #(.select(1), .width(32), .disabled("Z"), .enable("false")) multiplexer_10 (
    .in0({ram_1_data[31:16], regifile_1_r2}), .in1({regifile_1_r2, ram_1_data[15:0]}),
    .out(multiplexer_10_out), .sel(alu_1_result[1]));
  and and_2 (and_2_out, alu_1_equal, beq);
  or or_6 (or_6_out, comparator_1_gt, comparator_1_eq);
  Multiplexer #(.select(1), .width(32), .disabled("Z"), .enable("false")) multiplexer_11 (
    .in0(multiplexer_13_out), .in1(PC_4), .out(RDin), .sel(JJump));
  Adder #(.width(32)) adder_2 (.a(shifter_2_out), .b(PC), .out(adder_2_out), .cin(1'b0));  // open: cout
  Adder #(.width(32)) adder_3 (.a(shifter_3_out), .b(PC), .out(adder_3_out), .cin(1'b0));  // open: cout
  or or_7 (BJump, and_2_out, and_1_out, and_3_out);
  and and_3 (and_3_out, bge, or_6_out);
  RAM #(.addrWidth(10), .dataWidth(32), .bus("separate"), .Select("high")) ram_1 (
    .addr(alu_1_result_2), .din(MDin), .data(ram_1_data), .str(MemWrite), .clk(CLK));  // open: sel, ld, clr
  Multiplexer #(.select(1), .width(32), .disabled("Z"), .enable("false")) multiplexer_12 (
    .in0({alu_1_result[31:12], alu_1_result_2, alu_1_result[1:0]}), .in1(ram_1_data),
    .out(multiplexer_12_out), .sel(\单周期硬布线控制器_1_memtoreg ));
  Multiplexer #(.select(1), .width(32), .disabled("Z"), .enable("false")) multiplexer_13 (
    .in0(multiplexer_12_out), .in1(shifter_1_out), .out(multiplexer_13_out), .sel(lui));
  Comparator #(.width(32), .mode("twosComplement")) comparator_2 (
    .a(regifile_1_r1), .b(32'h22), .eq(comparator_2_eq));  // open: gt, lt
  not not_3 (not_3_out, comparator_2_eq);
  D_Flip_Flop #(.trigger("high"), .Pre_Clr_Positions("LEGACY"), .NegatePresetClear("false"), .enable("true"), .NewFFLayout("false")) d_ff_1 (.Q(d_ff_1_q));  // open: clk, D, Qn, preset, en, reset
  // Probe on 13'h609
  and and_4 (and_4_out, comparator_2_eq, ecall);
  and and_5 (and_5_out, not_3_out, ecall);
  Comparator #(.width(13), .mode("twosComplement")) comparator_3 (
    .a(CNT_num), .b(13'h609), .eq(comparator_3_eq), .lt(comparator_3_lt));  // open: gt
  Clock #(.highDuration(1), .lowDuration(1)) clock_1 (.out(clock_1_out));
  Register #(.width(32), .trigger("rising"), .Select("low")) register_1 (
    .D({regifile_1_r2_2, regifile_1_r2}), .en(and_4_out), .Q(LedData), .clk(CLK));  // open: clr
  Register #(.width(1), .trigger("falling"), .Select("low")) register_2 (
    .D(1'b1), .en(and_5_out), .Q(halt), .clk(CLK), .clr(Go));
  Counter #(.width(13), .max('h1fff), .ongoal("stay"), .trigger("rising"), .behavior("old")) counter_1 (
    .count(comparator_3_lt), .Q(CNT_num), .clk(clock_1_out));  // open: load, D, carry, clr, preset
  nand nand_1 (nand_1_out, d_ff_1_q, comparator_3_eq);
  assign CLK = nand_1_out ? clock_1_out : 1'bz;  // Controlled_Buffer controlled_buffer_1
  Pull_Resistor #(.pull(1)) pull_resistor_1 (.node(CLK));

  // Other names for the same wires on the sheet: NeedLink = JJump

  // Notes on the sheet:
  //   中断源
  //   中断等待指示
  //   数码管输出应该用寄存器锁存，否则显示数据只能一闪而过
  //   数码管输出
  //   指令探针
  //   指令存储器
  //   continue or jump
  //   指令字
  //   contents of rom_1 (hex, n*v repeats v):
  //   100493 100006f 100493 200913 300993 100006f 100493 200913 300993 100006f 100493 200913 300993
  //   100006f 100493 200913 300993 3b8000ef 100413 100493 1f49493 900533 2200893 73 24d493 48463 fedff06f
  //   900533 2200893 73 100493 249493 900533 2200893 73 48463 fedff06f 100493 1f49493 900533 2200893 73
  //   4034d493 900533 2200893 73 4044d493 900533 2200893 73 4044d493 900533 2200893 73 4044d493 900533
  //   2200893 73 4044d493 900533 2200893 73 4044d493 900533 2200893 73 4044d493 900533 2200893 73 4044d493
  //   900533 2200893 73 100413 1f41993 41f9d993 433 c00913 300b13 140413 f47413 800293 100313 499993
  //   89e9b3 1300533 2200893 73 406282b3 fe0294e3 140413 f00f93 1f47433 1c41413 800293 100313 49d993
  //   89e9b3 1300533 2200893 73 406282b3 fe0294e3 1c45413 406b0b33 b0463 f95ff06f 2b3 fff2c293 829293
  //   ff2e293 500533 2200893 73 fff00413 493 84a023 140413 448493 84a023 140413 448493 84a023 140413
  //   448493 84a023 140413 448493 84a023 140413 448493 84a023 140413 448493 84a023 140413 448493 84a023
  //   140413 448493 84a023 140413 448493 84a023 140413 448493 84a023 140413 448493 84a023 140413 448493
  //   84a023 140413 448493 84a023 140413 448493 84a023 140413 448493 84a023 140413 448493 140413 433
  //   3c00493 42983 4aa03 149a2b3 28663 134a023 1442023 ffc48493 fe9412e3 800533 2200893 73 440413 3c00493
  //   fc9416e3 100293 300313 800493 849493 7648493 1449493 900533 2200893 73 800e13 4054d4b3 4064d4b3
  //   900533 2200893 73 fffe0e13 fe0e14e3 a00893 73 800e13 fedc04b7 fff00413 1045413 84e4b3 900533 2200893
  //   73 ba984b7 900533 73 76544b7 900533 73 32104b7 900533 73 fffe0e13 fa0e1ee3 a00893 73 313 2000e13
  //   100493 100913 931023 900533 2200893 73 12484b3 230313 fffe0e13 fe0e12e3 1000e13 313 32483 900533
  //   2200893 73 430313 fffe0e13 fe0e14e3 a00893 73 f00493 900533 2200893 73 fff48493 fe04d8e3 a00893 73
  //   a00893 73 413 140413 800533 2200893 73 240413 800533 2200893 73 340413 800533 2200893 73 440413
  //   800533 2200893 73 540413 800533 2200893 73 640413 800533 2200893 73 740413 800533 2200893 73 840413
  //   800533 2200893 2200893 73 8067
  //   I
  //   URET
  //   S
  //   shamt
  //   B
  //   U
  //   J
  //   MemToReg
  //   j or b
  //   AluSrcB
  //   AluOP
  //   jal or jalr
  //   数据存储器
  //   data or RA
  //   为方便自动评测，需要输出PC，IR，寄存器堆写如数据RDin
  //   RAM写使能MemWrite、RAM写入数据MDin等信号
  //   from alu or mem
  //   控制位
  //   暂停节拍，不能为0
  //   戳工具置1进入计数暂停模式，ctrl+k时钟自动运行到对应节拍暂停
  //   ctrl+k关闭时钟连续运行，将控制位置零，进入单步调试模式调试
  //   用这个时钟源需要去掉电路中的其他时钟源
  //   可计数暂停的时钟源
endmodule

module \理想流水线  (
  output RegWrite,
  output MemWrite,
  output [31:0] IF_PC,
  output [31:0] ID_PC,
  output [31:0] EX_PC,
  output [31:0] M_PC,
  output [31:0] WB_PC,
  output [31:0] RDin,
  output [31:0] MDin,
  output [31:0] LedData
);

  wire alu_1_equal, and_1_out, and_3_out, and_4_out, and_5_out, asdasdasd, CLK, clock_1_out, comparator_1_eq,
       comparator_1_lt, comparator_2_eq, comparator_2_gt, comparator_3_eq, d_ff_1_q, EX_ALU_src, EX_beq,
       EX_bge, EX_BJump, EX_bne, EX_jal, EX_jalr, EX_JJump, ex_mem_1_ecall_out, ex_mem_1_regwrite_out, Go,
       halt, ID_ALU_src, ID_beq, ID_bge, ID_bne, ID_ecall, id_ex_1_ecall_out, id_ex_1_lui_out,
       id_ex_1_mem2reg_out, id_ex_1_memwrite_out, id_ex_1_regwrite_out, id_ex_1_sh_out, ID_jal, ID_jalr,
       ID_lui, ID_Mem2Reg, ID_MemWrite, ID_RegWrite, ID_sh, IR1, IR2, IR3, MEM_lui, MEM_Mem2Reg,
       MEM_NeedLink, MEM_sh, nand_1_out, not_1_out, not_2_out, not_3_out, or_1_out, or_2_out, or_3_out,
       riscv_probe_5_p1, RST, S, ShiftImm, W1, W2, W3, WB_ecall;
  wire [3:0] EX_ALU_op, ID_ALU_op;
  wire [4:0] ex_mem_1_regwritenum_out, id_ex_1_regwritenum_out, multiplexer_2_out, multiplexer_3_out,
       WB_RegWriteNum;
  wire [11:0] multiplexer_4_out;
  wire [12:0] CNT_num;
  wire [15:0] \LoadUse次数 , ram_1_data, ram_1_data_2, \总周期数 , \插入气泡数 , \无条件分支数 , \条件分支成功数 ;
  wire [31:0] adder_2_out, adder_3_out, adder_4_out, bit_extender_1_out, bit_extender_2_out,
       bit_extender_3_out, bit_extender_4_out, bit_extender_5_out, EX_ALU_res, EX_BImm, EX_IR, EX_ISImm,
       EX_JImm, ex_mem_1_rs1_out, EX_RS1, EX_RS2, id_ex_1_uimm_out, ID_IR, IF_IR, IF_PC_4, MEM_ALU_res,
       MEM_IR, MEM_RegData, MEM_RS2, MEM_UImm, multiplexer_1_out, multiplexer_5_out, multiplexer_6_out,
       multiplexer_7_out, multiplexer_8_out, multiplexer_11_out, multiplexer_12_out, multiplexer_13_out,
       regifile_1_r1, regifile_1_r2, shifter_1_out, shifter_2_out, shifter_3_out, WB_IR, WB_RS1, WB_RS2;

  Button \u_总复位  (.out(RST));
  Button _1 (.out(IR1));
  Button _2 (.out(IR2));
  Button _3 (.out(IR3));
  // Probe on \总周期数 
  // Probe on \总周期数 
  Button \u_继续运行  (.out(Go));
  LED #(.active("true")) led_1 (.in(W1));
  LED #(.active("true")) led_2 (.in(W2));
  LED #(.active("true")) led_3 (.in(W3));
  Register #(.width(32), .trigger("rising"), .Select("low")) PC (
    .D(multiplexer_1_out), .en(not_1_out), .Q(IF_PC), .clk(CLK), .clr(RST));
  not not_1 (not_1_out, halt);
  Hex_Digit_Display hex_digit_display_1 (.value(LedData[31:28]));  // open: dp
  // Probe on IF_PC[19:0]
  // RiscV_Probe riscv_probe_1: pin names not known; wires that end beside it: IF_IR
  Hex_Digit_Display hex_digit_display_2 (.value(LedData[23:20]));  // open: dp
  Hex_Digit_Display hex_digit_display_3 (.value(LedData[27:24]));  // open: dp
  // Probe on ID_PC[19:0]
  // RiscV_Probe riscv_probe_2: pin names not known; wires that end beside it: ID_IR
  Adder #(.width(32)) adder_1 (.a(32'h4), .b(IF_PC), .out(IF_PC_4), .cin(1'b0));  // open: cout
  Hex_Digit_Display hex_digit_display_4 (.value(LedData[15:12]));  // open: dp
  Hex_Digit_Display hex_digit_display_5 (.value(LedData[19:16]));  // open: dp
  Multiplexer #(.select(1), .width(32), .disabled("Z"), .enable("false")) multiplexer_1 (
    .in0(IF_PC_4), .in1(multiplexer_6_out), .out(multiplexer_1_out), .sel(or_1_out));
  Hex_Digit_Display hex_digit_display_6 (.value(LedData[11:8]));  // open: dp
  Hex_Digit_Display hex_digit_display_7 (.value(LedData[7:4]));  // open: dp
  // Probe on EX_PC[19:0]
  // RiscV_Probe riscv_probe_3: pin names not known; wires that end beside it: EX_IR
  ROM #(.addrWidth(10), .dataWidth(32), .Select("high")) rom_1 (.addr(IF_PC[11:2]), .data(IF_IR));
  Hex_Digit_Display hex_digit_display_8 (.value(LedData[3:0]));  // open: dp
  IF_ID if_id_1 (
    .IRin(IF_IR), .PCin(IF_PC), .CLK(CLK), .IRout(ID_IR), .PCout(ID_PC), .clear(1'b0), .halt(halt));  // open: Stall
  or or_1 (or_1_out, EX_JJump, EX_BJump);
  // Probe on \总周期数 
  // Probe on M_PC[19:0]
  // RiscV_Probe riscv_probe_4: pin names not known; wires that end beside it: MEM_IR
  // Probe on \总周期数 
  // Probe on \无条件分支数 
  // Probe on \条件分支成功数 
  // Probe on \插入气泡数 
  // Probe on \LoadUse次数 
  // Probe on IF_PC[11:0]
  // Probe on WB_PC[19:0]
  // RiscV_Probe riscv_probe_5: pin names not known; wires that end beside it: riscv_probe_5_p1, WB_IR
  \单周期硬布线控制器  \u_单周期硬布线控制器_1  (
    .Funct({ID_IR[30], ID_IR[25], ID_IR[14:12]}), .OP(ID_IR[6:2]), .ALU_OP(ID_ALU_op), .MemToReg(ID_Mem2Reg),
    .MemWrite(ID_MemWrite), .ALU_SRC(ID_ALU_src), .ecall(ID_ecall), .bge(ID_bge), .beq(ID_beq), .lui(ID_lui),
    .S_Type(S), .RegWrite(ID_RegWrite), .in_3(ID_IR[21]), .uret(riscv_probe_5_p1), .ShitfImm(ShiftImm),
    .bne(ID_bne), .jalr(ID_jalr), .jal(ID_jal), .sh(ID_sh));  // open: B_Type
  Multiplexer #(.select(1), .width(5), .disabled("Z"), .enable("false")) multiplexer_2 (
    .in0(ID_IR[19:15]), .in1(5'b10001), .out(multiplexer_2_out), .sel(ID_ecall));
  Multiplexer #(.select(1), .width(5), .disabled("Z"), .enable("false")) multiplexer_3 (
    .in0(ID_IR[24:20]), .in1(5'b01010), .out(multiplexer_3_out), .sel(ID_ecall));
  assign bit_extender_1_out = {{27{ID_IR[24]}}, ID_IR[24:20]};  // Bit_Extender bit_extender_1
  assign bit_extender_2_out = {{12{1'b0}}, ID_IR[31:12]};  // Bit_Extender bit_extender_2
  // Probe on ID_PC[11:0]
  // Probe on EX_PC[11:0]
  assign bit_extender_3_out = {{20{multiplexer_4_out[11]}}, multiplexer_4_out};  // Bit_Extender bit_extender_3
  Multiplexer #(.select(1), .width(12), .disabled("Z"), .enable("false")) multiplexer_4 (
    .in0(ID_IR[31:20]), .in1({ID_IR[31:25], ID_IR[11:7]}), .out(multiplexer_4_out), .sel(S));
  // Probe on M_PC[11:0]
  D_Flip_Flop #(.trigger("high"), .Pre_Clr_Positions("LEGACY"), .NegatePresetClear("false"), .enable("true"), .NewFFLayout("false")) d_ff_1 (.Q(d_ff_1_q));  // open: clk, D, Qn, preset, en, reset
  // Probe on 13'hc
  Regifile regifile_1 (
    .Din(RDin), .Clk(CLK), .R1(regifile_1_r1), .R2(regifile_1_r2), .WE(RegWrite), .W_num(WB_RegWriteNum),
    .R1_num(multiplexer_2_out), .R2_num(multiplexer_3_out));
  Multiplexer #(.select(1), .width(32), .disabled("Z"), .enable("false")) multiplexer_5 (
    .in0(bit_extender_3_out), .in1(bit_extender_1_out), .out(multiplexer_5_out), .sel(ShiftImm));
  Shifter #(.width(32), .shift("ll")) shifter_1 (.in(bit_extender_2_out), .\dist (5'b01100), .out(shifter_1_out));
  assign bit_extender_4_out = {{12{ID_IR[31]}}, {ID_IR[31], ID_IR[19:12], ID_IR[20], ID_IR[30:21]}};  // Bit_Extender bit_extender_4
  // Probe on WB_PC[11:0]
  Comparator #(.width(13), .mode("twosComplement")) comparator_1 (
    .a(CNT_num), .b(13'hc), .eq(comparator_1_eq), .lt(comparator_1_lt));  // open: gt
  Clock #(.highDuration(1), .lowDuration(1)) clock_1 (.out(clock_1_out));
  assign bit_extender_5_out = {{20{ID_IR[31]}}, {ID_IR[31], ID_IR[7], ID_IR[30:25], ID_IR[11:8]}};  // Bit_Extender bit_extender_5
  nand nand_1 (nand_1_out, d_ff_1_q, comparator_1_eq);
  Counter #(.width(13), .max('h1fff), .ongoal("stay"), .trigger("rising"), .behavior("old")) counter_1 (
    .count(comparator_1_lt), .Q(CNT_num), .clk(clock_1_out));  // open: load, D, carry, clr, preset
  assign CLK = nand_1_out ? clock_1_out : 1'bz;  // Controlled_Buffer controlled_buffer_1
  Pull_Resistor #(.pull(1)) pull_resistor_1 (.node(CLK));
  ID_EX id_ex_1 (
    .IRin(ID_IR), .IRout(EX_IR), .PCout(EX_PC), .RS1out(EX_RS1), .RS2out(EX_RS2), .Imm_out(EX_ISImm),
    .RegWrite_out(id_ex_1_regwrite_out), .MemWrite_out(id_ex_1_memwrite_out),
    .RegWriteNum_out(id_ex_1_regwritenum_out), .ALU_src_out(EX_ALU_src), .jal_out(EX_jal),
    .jalr_out(EX_jalr), .beq_out(EX_beq), .bne_out(EX_bne), .bge_out(EX_bge), .sh_out(id_ex_1_sh_out),
    .CLK(CLK), .lui_out(id_ex_1_lui_out), .ecall_out(id_ex_1_ecall_out), .Mem2Reg_out(id_ex_1_mem2reg_out),
    .BImm_out(EX_BImm), .UImm_out(id_ex_1_uimm_out), .JImm_out(EX_JImm), .ALU_op_out(EX_ALU_op),
    .PCin(ID_PC), .RS1in(regifile_1_r1), .RS2in(regifile_1_r2), .Imm_in(multiplexer_5_out),
    .RegWrite_in(ID_RegWrite), .MemWrite_in(ID_MemWrite), .RegWriteNum_in(ID_IR[11:7]),
    .ALU_src_in(ID_ALU_src), .jal_in(ID_jal), .jalr_in(ID_jalr), .beq_in(ID_beq), .bne_in(ID_bne),
    .bge_in(ID_bge), .sh_in(ID_sh), .lui_in(ID_lui), .ecall_in(ID_ecall), .Mem2Reg_in(ID_Mem2Reg),
    .BImm_in(bit_extender_5_out), .UImm_in(shifter_1_out), .JImm_in(bit_extender_4_out),
    .ALI_op_in(ID_ALU_op), .clear(1'b0), .halt(halt));
  Multiplexer #(.select(1), .width(32), .disabled("Z"), .enable("false")) multiplexer_6 (
    .in0(multiplexer_7_out), .in1(adder_2_out), .out(multiplexer_6_out), .sel(or_2_out));
  or or_2 (or_2_out, EX_bne, EX_beq, EX_bge);
  Shifter #(.width(32), .shift("ll")) shifter_2 (.in(EX_BImm), .\dist (5'b00001), .out(shifter_2_out));
  Shifter #(.width(32), .shift("ll")) shifter_3 (.in(EX_JImm), .\dist (5'b00001), .out(shifter_3_out));
  Multiplexer #(.select(1), .width(32), .disabled("Z"), .enable("false")) multiplexer_7 (
    .in0(adder_3_out), .in1(EX_ALU_res), .out(multiplexer_7_out), .sel(EX_jalr));
  Adder #(.width(32)) adder_2 (.a(shifter_2_out), .b(EX_PC), .out(adder_2_out), .cin(1'b0));  // open: cout
  Adder #(.width(32)) adder_3 (.a(shifter_3_out), .b(EX_PC), .out(adder_3_out), .cin(1'b0));  // open: cout
  Multiplexer #(.select(1), .width(32), .disabled("Z"), .enable("false")) multiplexer_8 (
    .in0(EX_RS2), .in1(EX_ISImm), .out(multiplexer_8_out), .sel(EX_ALU_src));
  ALU alu_1 (
    .X(EX_RS1), .Y(multiplexer_8_out), .AluOP(EX_ALU_op), .Equal(alu_1_equal), .Result(EX_ALU_res));  // open: Result_2, out_4, out_6
  and and_1 (and_1_out, alu_1_equal, EX_beq);
  not not_2 (not_2_out, alu_1_equal);
  and and_2 (and_1_out, not_2_out, EX_bne);
  Comparator #(.width(32), .mode("twosComplement")) comparator_2 (
    .a(EX_RS1), .b(EX_RS2), .gt(comparator_2_gt), .eq(comparator_2_eq));  // open: lt
  and and_3 (and_3_out, EX_bge, or_3_out);
  or or_3 (or_3_out, comparator_2_gt, comparator_2_eq);
  or or_4 (EX_JJump, EX_jal, EX_jalr);
  or or_5 (EX_BJump, and_1_out, and_1_out, and_3_out);
  or or_6 (asdasdasd, EX_JJump, EX_BJump);
  EX_MEM ex_mem_1 (
    .IR_in(EX_IR), .PC_in(EX_PC), .RS1_in(EX_RS1), .RS2_in(EX_RS2), .UImm_in(id_ex_1_uimm_out),
    .ALU_result_in(EX_ALU_res), .NeedLink_in(EX_JJump), .RegWrite_in(id_ex_1_regwrite_out),
    .MemWrite_in(id_ex_1_memwrite_out), .RegWriteNum_in(id_ex_1_regwritenum_out), .lui_in(id_ex_1_lui_out),
    .ecall_in(id_ex_1_ecall_out), .sh_in(id_ex_1_sh_out), .Mem2Reg_in(id_ex_1_mem2reg_out), .CLK(CLK),
    .IR_out(MEM_IR), .PC_out(M_PC), .RS1_out(ex_mem_1_rs1_out), .RS2_out(MEM_RS2), .UImm_out(MEM_UImm),
    .ALU_result_out(MEM_ALU_res), .NeedLink_out(MEM_NeedLink), .RegWrite_out(ex_mem_1_regwrite_out),
    .MemWrite_out(MemWrite), .RegWriteNum_out(ex_mem_1_regwritenum_out), .lui_out(MEM_lui),
    .ecall_out(ex_mem_1_ecall_out), .sh_out(MEM_sh), .Mem2Reg_out(MEM_Mem2Reg), .halt(halt));
  Multiplexer #(.select(1), .width(32), .disabled("Z"), .enable("false")) multiplexer_9 (
    .in0(MEM_RS2), .in1(multiplexer_11_out), .out(MDin), .sel(MEM_sh));
  Multiplexer #(.select(1), .width(32), .disabled("Z"), .enable("false")) multiplexer_10 (
    .in0(multiplexer_13_out), .in1(adder_4_out), .out(MEM_RegData), .sel(MEM_NeedLink));
  Adder #(.width(32)) adder_4 (.a(32'h4), .b(M_PC), .out(adder_4_out));  // open: cin, cout
  RAM #(.addrWidth(10), .dataWidth(32), .bus("separate"), .Select("high")) ram_1 (
    .addr(MEM_ALU_res[11:2]), .din(MDin), .data({ram_1_data_2, ram_1_data}), .str(MemWrite), .clk(CLK));  // open: sel, ld, clr
  Multiplexer #(.select(1), .width(32), .disabled("Z"), .enable("false")) multiplexer_11 (
    .in0({ram_1_data_2, MEM_RS2[15:0]}), .in1({MEM_RS2[15:0], ram_1_data}), .out(multiplexer_11_out),
    .sel(MEM_ALU_res[1]));
  Multiplexer #(.select(1), .width(32), .disabled("Z"), .enable("false")) multiplexer_12 (
    .in0(MEM_ALU_res), .in1({ram_1_data_2, ram_1_data}), .out(multiplexer_12_out), .sel(MEM_Mem2Reg));
  Multiplexer #(.select(1), .width(32), .disabled("Z"), .enable("false")) multiplexer_13 (
    .in0(multiplexer_12_out), .in1(MEM_UImm), .out(multiplexer_13_out), .sel(MEM_lui));
  MEM_WB mem_wb_1 (
    .IR_in(MEM_IR), .PC_in(M_PC), .RS1_in(ex_mem_1_rs1_out), .RS2_out(MEM_RS2), .RegData_in(MEM_RegData),
    .CLK(CLK), .IR_out(WB_IR), .PC_out(WB_PC), .RS1_out(WB_RS1), .RS2_out_2(WB_RS2), .RegData_out(RDin),
    .halt(halt), .RegWrite_in(ex_mem_1_regwrite_out), .RegWrite_out(RegWrite),
    .RegWriteNum_in(ex_mem_1_regwritenum_out), .RegWriteNum_out(WB_RegWriteNum),
    .ecall_in(ex_mem_1_ecall_out), .ecall_out(WB_ecall));  // open: MemData_in, MemData_out, MemWrite_in, MemWrite_out, MemWriteAddr_in, MemWriteAddr_out
  Comparator #(.width(32), .mode("twosComplement")) comparator_3 (
    .a(WB_RS1), .b(32'h22), .eq(comparator_3_eq));  // open: gt, lt
  not not_3 (not_3_out, comparator_3_eq);
  and and_4 (and_4_out, comparator_3_eq, WB_ecall);
  and and_5 (and_5_out, not_3_out, WB_ecall);
  Register #(.width(1), .trigger("falling"), .Select("low")) register_1 (
    .D(1'b1), .en(and_5_out), .Q(halt), .clk(CLK), .clr(Go));
  Register #(.width(32), .trigger("rising"), .Select("low")) register_2 (
    .D(WB_RS2), .en(and_4_out), .Q(LedData), .clk(CLK));  // open: clr

  // Other names for the same wires on the sheet: MEM_MemData[31:0] = MDin; MEM_MemWrite = MemWrite;
  //   MEM_PC[31:0] = M_PC; WB_RegData[31:0] = RDin; WB_RegWrite = RegWrite

  // Notes on the sheet:
  //   中断源
  //   时空图监测，可删除
  //   中断等待指示
  //   数码管输出
  //   指令存储器
  //   continue or jump
  //   contents of rom_1 (hex, n*v repeats v):
  //   413 493 913 993 46413 14e493 296913 39e993 842023 942223 1242423 1342623 a00893 493 913 993 73
  //   URET
  //   I
  //   S
  //   shamt
  //   B
  //   U
  //   J
  //   控制位
  //   流水调试日志用
  //   暂停节拍，不能为0
  //   戳工具置1进入计数暂停模式，ctrl+k时钟自动运行到对应节拍暂停
  //   ctrl+k关闭时钟连续运行，将控制位置零，进入单步调试模式调试
  //   用这个时钟源需要去掉电路中的其他时钟源
  //   可计数暂停的时钟源
  //   j or b
  //   为方便自动评测，需要输出流水线各段保存的PC值，注意是PC不是PC+4，另外ID段寄存器写入信息，Mem段内存写入信息也要输出
  //   jal or jalr
  //   AluSrcB
  //   data or RA
  //   数据存储器
  //   from alu or mem
endmodule

// 单周期硬布线控制器
module \单周期硬布线控制器  (
  input  [4:0] OP,
  input  [4:0] Funct,
  input  in_3,
  output [3:0] ALU_OP,
  output uret,
  output MemToReg,
  output ecall,
  output MemWrite,
  output ALU_SRC,
  output B_Type,
  output ShitfImm,
  output bge,
  output lui,
  output RegWrite,
  output S_Type,
  output beq,
  output bne,
  output jalr,
  output jal,
  output sh
);

  wire \控制信号自动生成_1_ecall ;

  \运算控制器自动生成  \u_运算控制器自动生成_1  (
    .OP2(OP[0]), .OP3(OP[1]), .OP4(OP[2]), .OP5(OP[3]), .OP6(OP[4]), .F12(Funct[0]), .F13(Funct[1]),
    .F14(Funct[2]), .F25(Funct[3]), .F30(Funct[4]), .S0(ALU_OP[0]), .S1(ALU_OP[1]), .S2(ALU_OP[2]),
    .S3(ALU_OP[3]));
  \控制信号自动生成  \u_控制信号自动生成_1  (
    .OP2(OP[0]), .OP3(OP[1]), .MemToReg(MemToReg), .OP4(OP[2]), .OP5(OP[3]), .OP6(OP[4]), .F12(Funct[0]),
    .F13(Funct[1]), .F14(Funct[2]), .MemWrite(MemWrite), .F25(Funct[3]), .F30(Funct[4]), .ALU_SRC(ALU_SRC),
    .B_Type(B_Type), .ShiftImm(ShitfImm), .bge(bge), .lui(lui), .RegWrite(RegWrite),
    .ecall(\控制信号自动生成_1_ecall ), .S_Type(S_Type), .BEQ(beq), .BNE(bne), .JALR(jalr), .JAL(jal), .sh(sh));
  and and_1 (uret, in_3, \控制信号自动生成_1_ecall );
  and and_2 (ecall, ~in_3, \控制信号自动生成_1_ecall );  // AND_Gate

  // Other names for the same wires on the sheet: IR21 = in_3; OP_CODE[4:0] = OP

  // Notes on the sheet:
  //   控制信号生成，产生数据通路需要的其他控制信号
  //   运算器控制器，根据指令生成运算器功能选择信号
endmodule

// 运算器控制器
module \运算控制器自动生成  (
  input  OP2,
  input  OP3,
  input  OP4,
  input  OP5,
  input  OP6,
  input  F12,
  input  F13,
  input  F14,
  input  F25,
  input  F30,
  output S0,
  output S1,
  output S2,
  output S3
);

  wire and_1_out, and_2_out, and_3_out, and_4_out, and_5_out, and_6_out, and_7_out, and_8_out, and_9_out,
       and_10_out, and_11_out, and_12_out, and_13_out, and_14_out, and_15_out, and_16_out, and_17_out,
       and_18_out, and_19_out, and_20_out, and_21_out, and_22_out, and_23_out, and_24_out, and_25_out,
       and_26_out, and_27_out, and_28_out, and_29_out, and_30_out, and_31_out, and_32_out, and_33_out,
       and_34_out, and_35_out, and_36_out, and_37_out, not_1_out, not_2_out, not_3_out, not_4_out, not_5_out,
       not_6_out, not_7_out, not_8_out, not_9_out, not_10_out, not_11_out, not_12_out, not_13_out,
       not_14_out, not_15_out, not_16_out, not_17_out, not_18_out, not_19_out, not_20_out, not_21_out,
       not_22_out, not_23_out, not_24_out, not_25_out, not_26_out, not_27_out, not_28_out, not_29_out,
       not_30_out, not_31_out, not_32_out, not_33_out, not_34_out, not_35_out, not_36_out, not_37_out,
       not_38_out, not_39_out, not_40_out, not_41_out, not_42_out, not_43_out, not_44_out, not_45_out,
       not_46_out, not_47_out, not_48_out, not_49_out, not_50_out, not_51_out, not_52_out, not_53_out,
       not_54_out, not_55_out, not_56_out, not_57_out, not_58_out, not_59_out, not_60_out, not_61_out,
       not_62_out, not_63_out, not_64_out, not_65_out, not_66_out, not_67_out, not_68_out, not_69_out,
       not_70_out, not_71_out, not_72_out, not_73_out, not_74_out, not_75_out, not_76_out, not_77_out,
       not_78_out, not_79_out, not_80_out, not_81_out, not_82_out, not_83_out, not_84_out, not_85_out,
       not_86_out, not_87_out, not_88_out, not_89_out, not_90_out, not_91_out, not_92_out, not_93_out,
       not_94_out, not_95_out, not_96_out, not_97_out, not_98_out, not_99_out, not_100_out, not_101_out,
       not_102_out, not_103_out, not_104_out, not_105_out, not_106_out, not_107_out, not_108_out,
       not_109_out, not_110_out, not_111_out, not_112_out, not_113_out, not_114_out, not_115_out,
       not_116_out, not_117_out, not_118_out, not_119_out, not_120_out, not_121_out, not_122_out,
       not_123_out, not_124_out, not_125_out, not_126_out, not_127_out, not_128_out, not_129_out,
       not_130_out, not_131_out, not_132_out, not_133_out, not_134_out, not_135_out, not_136_out,
       not_137_out, not_138_out, not_139_out, not_140_out, not_141_out, not_142_out, not_143_out,
       not_144_out, not_145_out, not_146_out, not_147_out, not_148_out, not_149_out, not_150_out,
       not_151_out, not_152_out, not_153_out, not_154_out, not_155_out, not_156_out, not_157_out,
       not_158_out, not_159_out, not_160_out, not_161_out, not_162_out, not_163_out, not_164_out,
       not_165_out, not_166_out, not_167_out, not_168_out, not_169_out, not_170_out, not_171_out,
       not_172_out, not_173_out, not_174_out, not_175_out, not_176_out, not_177_out, not_178_out,
       not_179_out, not_180_out, not_181_out, not_182_out, not_183_out, not_184_out, not_185_out,
       not_186_out, not_187_out, not_188_out, not_189_out, not_190_out, not_191_out, not_192_out,
       not_193_out, not_194_out, not_195_out, not_196_out, not_197_out, not_198_out, not_199_out,
       not_200_out, not_201_out, not_202_out, not_203_out, not_204_out, not_205_out, not_206_out,
       not_207_out, not_208_out, not_209_out, not_210_out, not_211_out, not_212_out, not_213_out,
       not_214_out, not_215_out, not_216_out, not_217_out, not_218_out, not_219_out;

  not not_1 (not_1_out, F30);
  not not_2 (not_2_out, F25);
  not not_3 (not_3_out, F14);
  not not_4 (not_4_out, F13);
  not not_5 (not_5_out, F12);
  not not_6 (not_6_out, OP6);
  not not_7 (not_7_out, OP3);
  not not_8 (not_8_out, OP2);
  not not_9 (not_9_out, F30);
  not not_10 (not_10_out, F25);
  not not_11 (not_11_out, OP6);
  not not_12 (not_12_out, OP3);
  not not_13 (not_13_out, OP2);
  not not_14 (not_14_out, F30);
  not not_15 (not_15_out, F25);
  not not_16 (not_16_out, F14);
  not not_17 (not_17_out, F12);
  not not_18 (not_18_out, OP6);
  not not_19 (not_19_out, OP3);
  not not_20 (not_20_out, OP2);
  not not_21 (not_21_out, F14);
  not not_22 (not_22_out, F13);
  not not_23 (not_23_out, F12);
  not not_24 (not_24_out, OP6);
  not not_25 (not_25_out, OP5);
  not not_26 (not_26_out, OP3);
  not not_27 (not_27_out, OP2);
  not not_28 (not_28_out, OP6);
  not not_29 (not_29_out, OP5);
  not not_30 (not_30_out, OP3);
  not not_31 (not_31_out, OP2);
  not not_32 (not_32_out, F13);
  not not_33 (not_33_out, F12);
  not not_34 (not_34_out, OP6);
  not not_35 (not_35_out, OP5);
  not not_36 (not_36_out, OP3);
  not not_37 (not_37_out, OP2);
  not not_38 (not_38_out, F14);
  not not_39 (not_39_out, F12);
  not not_40 (not_40_out, OP6);
  not not_41 (not_41_out, OP5);
  not not_42 (not_42_out, OP3);
  not not_43 (not_43_out, OP2);
  not not_44 (not_44_out, F25);
  not not_45 (not_45_out, F13);
  not not_46 (not_46_out, OP6);
  not not_47 (not_47_out, OP5);
  not not_48 (not_48_out, OP3);
  not not_49 (not_49_out, OP2);
  not not_50 (not_50_out, F14);
  not not_51 (not_51_out, F12);
  not not_52 (not_52_out, OP6);
  not not_53 (not_53_out, OP5);
  not not_54 (not_54_out, OP4);
  not not_55 (not_55_out, OP3);
  not not_56 (not_56_out, OP2);
  not not_57 (not_57_out, F14);
  not not_58 (not_58_out, F12);
  not not_59 (not_59_out, OP6);
  not not_60 (not_60_out, OP4);
  not not_61 (not_61_out, OP3);
  not not_62 (not_62_out, OP2);
  not not_63 (not_63_out, F14);
  not not_64 (not_64_out, F13);
  not not_65 (not_65_out, F12);
  not not_66 (not_66_out, OP4);
  not not_67 (not_67_out, OP3);
  not not_68 (not_68_out, F25);
  not not_69 (not_69_out, F13);
  not not_70 (not_70_out, OP6);
  not not_71 (not_71_out, OP3);
  not not_72 (not_72_out, OP2);
  not not_73 (not_73_out, F14);
  not not_74 (not_74_out, F13);
  not not_75 (not_75_out, OP6);
  not not_76 (not_76_out, OP4);
  not not_77 (not_77_out, OP3);
  not not_78 (not_78_out, OP2);
  not not_79 (not_79_out, F25);
  not not_80 (not_80_out, F14);
  not not_81 (not_81_out, F13);
  not not_82 (not_82_out, F12);
  not not_83 (not_83_out, OP6);
  not not_84 (not_84_out, OP3);
  not not_85 (not_85_out, OP2);
  not not_86 (not_86_out, F30);
  not not_87 (not_87_out, F25);
  not not_88 (not_88_out, OP6);
  not not_89 (not_89_out, OP3);
  not not_90 (not_90_out, OP2);
  not not_91 (not_91_out, F30);
  not not_92 (not_92_out, F25);
  not not_93 (not_93_out, F14);
  not not_94 (not_94_out, F12);
  not not_95 (not_95_out, OP6);
  not not_96 (not_96_out, OP3);
  not not_97 (not_97_out, OP2);
  not not_98 (not_98_out, OP6);
  not not_99 (not_99_out, OP5);
  not not_100 (not_100_out, OP3);
  not not_101 (not_101_out, OP2);
  not not_102 (not_102_out, F14);
  not not_103 (not_103_out, F12);
  not not_104 (not_104_out, OP6);
  not not_105 (not_105_out, OP5);
  not not_106 (not_106_out, OP3);
  not not_107 (not_107_out, OP2);
  not not_108 (not_108_out, F30);
  not not_109 (not_109_out, F25);
  not not_110 (not_110_out, F13);
  not not_111 (not_111_out, OP6);
  not not_112 (not_112_out, OP5);
  not not_113 (not_113_out, OP3);
  not not_114 (not_114_out, OP2);
  not not_115 (not_115_out, F13);
  not not_116 (not_116_out, OP4);
  not not_117 (not_117_out, OP3);
  not not_118 (not_118_out, OP2);
  not not_119 (not_119_out, F30);
  not not_120 (not_120_out, F25);
  not not_121 (not_121_out, F14);
  not not_122 (not_122_out, F13);
  not not_123 (not_123_out, F12);
  not not_124 (not_124_out, OP6);
  not not_125 (not_125_out, OP3);
  not not_126 (not_126_out, OP2);
  not not_127 (not_127_out, F25);
  not not_128 (not_128_out, F14);
  not not_129 (not_129_out, F13);
  not not_130 (not_130_out, F12);
  not not_131 (not_131_out, OP6);
  not not_132 (not_132_out, OP3);
  not not_133 (not_133_out, OP2);
  not not_134 (not_134_out, F30);
  not not_135 (not_135_out, F25);
  not not_136 (not_136_out, OP6);
  not not_137 (not_137_out, OP3);
  not not_138 (not_138_out, OP2);
  not not_139 (not_139_out, F30);
  not not_140 (not_140_out, F25);
  not not_141 (not_141_out, F14);
  not not_142 (not_142_out, OP6);
  not not_143 (not_143_out, OP3);
  not not_144 (not_144_out, OP2);
  not not_145 (not_145_out, F14);
  not not_146 (not_146_out, F13);
  not not_147 (not_147_out, F12);
  not not_148 (not_148_out, OP6);
  not not_149 (not_149_out, OP5);
  not not_150 (not_150_out, OP3);
  not not_151 (not_151_out, OP2);
  not not_152 (not_152_out, OP6);
  not not_153 (not_153_out, OP5);
  not not_154 (not_154_out, OP3);
  not not_155 (not_155_out, OP2);
  not not_156 (not_156_out, F14);
  not not_157 (not_157_out, F12);
  not not_158 (not_158_out, OP6);
  not not_159 (not_159_out, OP5);
  not not_160 (not_160_out, OP4);
  not not_161 (not_161_out, OP3);
  not not_162 (not_162_out, OP2);
  not not_163 (not_163_out, F14);
  not not_164 (not_164_out, F12);
  not not_165 (not_165_out, OP6);
  not not_166 (not_166_out, OP4);
  not not_167 (not_167_out, OP3);
  not not_168 (not_168_out, OP2);
  not not_169 (not_169_out, F14);
  not not_170 (not_170_out, F13);
  not not_171 (not_171_out, F12);
  not not_172 (not_172_out, OP4);
  not not_173 (not_173_out, OP3);
  not not_174 (not_174_out, F14);
  not not_175 (not_175_out, F13);
  not not_176 (not_176_out, OP6);
  not not_177 (not_177_out, OP4);
  not not_178 (not_178_out, OP3);
  not not_179 (not_179_out, OP2);
  not not_180 (not_180_out, F13);
  not not_181 (not_181_out, OP4);
  not not_182 (not_182_out, OP3);
  not not_183 (not_183_out, OP2);
  not not_184 (not_184_out, F30);
  not not_185 (not_185_out, F25);
  not not_186 (not_186_out, F12);
  not not_187 (not_187_out, OP6);
  not not_188 (not_188_out, OP3);
  not not_189 (not_189_out, OP2);
  not not_190 (not_190_out, F30);
  not not_191 (not_191_out, F25);
  not not_192 (not_192_out, F14);
  not not_193 (not_193_out, F12);
  not not_194 (not_194_out, OP6);
  not not_195 (not_195_out, OP3);
  not not_196 (not_196_out, OP2);
  not not_197 (not_197_out, F30);
  not not_198 (not_198_out, F25);
  not not_199 (not_199_out, F14);
  not not_200 (not_200_out, OP6);
  not not_201 (not_201_out, OP3);
  not not_202 (not_202_out, OP2);
  not not_203 (not_203_out, F12);
  not not_204 (not_204_out, OP6);
  not not_205 (not_205_out, OP5);
  not not_206 (not_206_out, OP3);
  not not_207 (not_207_out, OP2);
  not not_208 (not_208_out, F13);
  not not_209 (not_209_out, F12);
  not not_210 (not_210_out, OP6);
  not not_211 (not_211_out, OP5);
  not not_212 (not_212_out, OP3);
  not not_213 (not_213_out, OP2);
  not not_214 (not_214_out, F14);
  not not_215 (not_215_out, F12);
  not not_216 (not_216_out, OP6);
  not not_217 (not_217_out, OP5);
  not not_218 (not_218_out, OP3);
  not not_219 (not_219_out, OP2);
  and and_1 (and_1_out, not_1_out, not_2_out, not_3_out, not_4_out, not_5_out, not_6_out, OP5, OP4, not_7_out, not_8_out);
  and and_2 (and_2_out, not_9_out, not_10_out, F14, F13, F12, not_11_out, OP5, OP4, not_12_out, not_13_out);
  and and_3 (and_3_out, not_14_out, not_15_out, not_16_out, F13, not_17_out, not_18_out, OP5, OP4, not_19_out, not_20_out);
  and and_4 (and_4_out, not_21_out, not_22_out, not_23_out, not_24_out, not_25_out, OP4, not_26_out, not_27_out);
  and and_5 (and_5_out, F14, F13, F12, not_28_out, not_29_out, OP4, not_30_out, not_31_out);
  and and_6 (and_6_out, F14, not_32_out, not_33_out, not_34_out, not_35_out, OP4, not_36_out, not_37_out);
  and and_7 (and_7_out, not_38_out, F13, not_39_out, not_40_out, not_41_out, OP4, not_42_out, not_43_out);
  and and_8 (and_8_out, F30, not_44_out, F14, not_45_out, F12, not_46_out, not_47_out, OP4, not_48_out, not_49_out);
  and and_9 (and_9_out, not_50_out, F13, not_51_out, not_52_out, not_53_out, not_54_out, not_55_out, not_56_out);
  and and_10 (and_10_out, not_57_out, F13, not_58_out, not_59_out, OP5, not_60_out, not_61_out, not_62_out);
  and and_11 (and_11_out, not_63_out, not_64_out, not_65_out, OP6, OP5, not_66_out, not_67_out, OP2);
  and and_12 (and_12_out, F30, not_68_out, F14, not_69_out, F12, not_70_out, OP5, OP4, not_71_out, not_72_out);
  and and_13 (and_13_out, not_73_out, not_74_out, F12, not_75_out, OP5, not_76_out, not_77_out, not_78_out);
  and and_14 (and_14_out, F30, not_79_out, not_80_out, not_81_out, not_82_out, not_83_out, OP5, OP4, not_84_out, not_85_out);
  and and_15 (and_15_out, not_86_out, not_87_out, F14, F13, F12, not_88_out, OP5, OP4, not_89_out, not_90_out);
  and and_16 (and_16_out, not_91_out, not_92_out, not_93_out, F13, not_94_out, not_95_out, OP5, OP4, not_96_out, not_97_out);
  and and_17 (and_17_out, F14, F13, F12, not_98_out, not_99_out, OP4, not_100_out, not_101_out);
  and and_18 (and_18_out, not_102_out, F13, not_103_out, not_104_out, not_105_out, OP4, not_106_out, not_107_out);
  and and_19 (and_19_out, not_108_out, not_109_out, F14, not_110_out, F12, not_111_out, not_112_out, OP4, not_113_out, not_114_out);
  and and_20 (and_20_out, F14, not_115_out, F12, OP6, OP5, not_116_out, not_117_out, not_118_out);
  and and_21 (and_21_out, not_119_out, not_120_out, not_121_out, not_122_out, not_123_out, not_124_out, OP5, OP4, not_125_out, not_126_out);
  and and_22 (and_22_out, F30, not_127_out, not_128_out, not_129_out, not_130_out, not_131_out, OP5, OP4, not_132_out, not_133_out);
  and and_23 (and_23_out, not_134_out, not_135_out, F14, F13, F12, not_136_out, OP5, OP4, not_137_out, not_138_out);
  and and_24 (and_24_out, not_139_out, not_140_out, not_141_out, F13, F12, not_142_out, OP5, OP4, not_143_out, not_144_out);
  and and_25 (and_25_out, not_145_out, not_146_out, not_147_out, not_148_out, not_149_out, OP4, not_150_out, not_151_out);
  and and_26 (and_26_out, F14, F13, F12, not_152_out, not_153_out, OP4, not_154_out, not_155_out);
  and and_27 (and_27_out, not_156_out, F13, not_157_out, not_158_out, not_159_out, not_160_out, not_161_out, not_162_out);
  and and_28 (and_28_out, not_163_out, F13, not_164_out, not_165_out, OP5, not_166_out, not_167_out, not_168_out);
  and and_29 (and_29_out, not_169_out, not_170_out, not_171_out, OP6, OP5, not_172_out, not_173_out, OP2);
  and and_30 (and_30_out, not_174_out, not_175_out, F12, not_176_out, OP5, not_177_out, not_178_out, not_179_out);
  and and_31 (and_31_out, F14, not_180_out, F12, OP6, OP5, not_181_out, not_182_out, not_183_out);
  and and_32 (and_32_out, not_184_out, not_185_out, F14, F13, not_186_out, not_187_out, OP5, OP4, not_188_out, not_189_out);
  and and_33 (and_33_out, not_190_out, not_191_out, not_192_out, F13, not_193_out, not_194_out, OP5, OP4, not_195_out, not_196_out);
  and and_34 (and_34_out, not_197_out, not_198_out, not_199_out, F13, F12, not_200_out, OP5, OP4, not_201_out, not_202_out);
  and and_35 (and_35_out, F14, F13, not_203_out, not_204_out, not_205_out, OP4, not_206_out, not_207_out);
  and and_36 (and_36_out, F14, not_208_out, not_209_out, not_210_out, not_211_out, OP4, not_212_out, not_213_out);
  and and_37 (and_37_out, not_214_out, F13, not_215_out, not_216_out, not_217_out, OP4, not_218_out, not_219_out);
  or or_1 (S0, and_1_out, and_2_out, and_3_out, and_4_out, and_5_out, and_6_out, and_7_out, and_8_out, and_9_out, and_10_out, and_11_out, and_12_out, and_13_out);
  or or_2 (S1, and_14_out, and_15_out, and_16_out, and_17_out, and_18_out, and_19_out, and_20_out);
  or or_3 (S2, and_21_out, and_22_out, and_23_out, and_24_out, and_25_out, and_26_out, and_27_out, and_28_out, and_29_out, and_30_out, and_31_out);
  or or_4 (S3, and_32_out, and_33_out, and_34_out, and_35_out, and_36_out, and_37_out);
endmodule
// 控制信号生成
module \控制信号自动生成  (
  input  OP2,
  input  OP3,
  input  OP4,
  input  OP5,
  input  OP6,
  input  F12,
  input  F13,
  input  F14,
  input  F25,
  input  F30,
  output MemToReg,
  output MemWrite,
  output ALU_SRC,
  output B_Type,
  output ShiftImm,
  output bge,
  output lui,
  output RegWrite,
  output ecall,
  output S_Type,
  output BEQ,
  output BNE,
  output JALR,
  output JAL,
  output sh
);

  wire and_2_out, and_3_out, and_4_out, and_5_out, and_6_out, and_7_out, and_8_out, and_9_out, and_10_out,
       and_11_out, and_12_out, and_13_out, and_14_out, and_15_out, and_16_out, and_17_out, and_18_out,
       and_19_out, and_20_out, and_21_out, and_24_out, and_25_out, and_26_out, and_27_out, and_28_out,
       and_29_out, and_30_out, and_31_out, and_32_out, and_33_out, and_34_out, and_35_out, and_36_out,
       and_37_out, and_38_out, and_39_out, and_40_out, and_41_out, and_42_out, and_44_out, and_45_out,
       not_1_out, not_2_out, not_3_out, not_4_out, not_5_out, not_6_out, not_7_out, not_8_out, not_9_out,
       not_10_out, not_11_out, not_12_out, not_13_out, not_14_out, not_15_out, not_16_out, not_17_out,
       not_18_out, not_19_out, not_20_out, not_21_out, not_22_out, not_23_out, not_24_out, not_25_out,
       not_26_out, not_27_out, not_28_out, not_29_out, not_30_out, not_31_out, not_32_out, not_33_out,
       not_34_out, not_35_out, not_36_out, not_37_out, not_38_out, not_39_out, not_40_out, not_41_out,
       not_42_out, not_43_out, not_44_out, not_45_out, not_46_out, not_47_out, not_48_out, not_49_out,
       not_50_out, not_51_out, not_52_out, not_53_out, not_54_out, not_55_out, not_56_out, not_57_out,
       not_58_out, not_59_out, not_60_out, not_61_out, not_62_out, not_63_out, not_64_out, not_65_out,
       not_66_out, not_67_out, not_68_out, not_69_out, not_70_out, not_71_out, not_72_out, not_73_out,
       not_74_out, not_75_out, not_76_out, not_77_out, not_78_out, not_79_out, not_80_out, not_81_out,
       not_82_out, not_83_out, not_84_out, not_85_out, not_86_out, not_87_out, not_88_out, not_89_out,
       not_90_out, not_91_out, not_92_out, not_93_out, not_94_out, not_95_out, not_96_out, not_97_out,
       not_98_out, not_99_out, not_100_out, not_101_out, not_102_out, not_103_out, not_104_out, not_105_out,
       not_106_out, not_107_out, not_108_out, not_109_out, not_110_out, not_111_out, not_112_out,
       not_113_out, not_114_out, not_115_out, not_116_out, not_117_out, not_118_out, not_119_out,
       not_120_out, not_121_out, not_122_out, not_123_out, not_124_out, not_125_out, not_126_out,
       not_127_out, not_128_out, not_129_out, not_130_out, not_131_out, not_132_out, not_133_out,
       not_134_out, not_135_out, not_136_out, not_137_out, not_138_out, not_139_out, not_140_out,
       not_141_out, not_142_out, not_143_out, not_144_out, not_145_out, not_146_out, not_147_out,
       not_148_out, not_149_out, not_150_out, not_151_out, not_152_out, not_153_out, not_154_out,
       not_155_out, not_156_out, not_157_out, not_158_out, not_159_out, not_160_out, not_161_out,
       not_162_out, not_163_out, not_164_out, not_165_out, not_166_out, not_167_out, not_168_out,
       not_169_out, not_170_out, not_171_out, not_172_out, not_173_out, not_174_out, not_175_out,
       not_176_out, not_177_out, not_178_out, not_179_out, not_180_out, not_181_out, not_182_out,
       not_183_out, not_184_out, not_185_out, not_186_out, not_187_out, not_188_out, not_189_out,
       not_190_out, not_191_out, not_192_out, not_193_out, not_194_out, not_195_out, not_196_out,
       not_197_out, not_198_out, not_199_out, not_200_out, not_201_out, not_202_out, not_203_out,
       not_204_out, not_205_out, not_206_out, not_207_out, not_208_out, not_209_out, not_210_out,
       not_211_out, not_212_out, not_213_out, not_214_out, not_215_out, not_216_out, not_217_out,
       not_218_out, not_219_out, not_220_out, not_221_out, not_222_out, not_223_out, not_224_out,
       not_225_out, not_226_out, not_227_out, not_228_out, not_229_out, not_230_out, not_231_out,
       not_232_out, not_233_out, not_234_out, not_235_out, not_236_out, not_237_out, not_238_out,
       not_239_out, not_240_out, not_241_out, not_242_out, not_243_out, not_244_out, not_245_out,
       not_246_out, not_247_out, not_248_out, not_249_out, not_250_out, not_251_out, not_252_out,
       not_253_out, not_254_out, not_255_out, not_256_out, not_257_out, not_258_out, not_259_out,
       not_260_out, not_261_out, not_262_out, not_263_out, not_264_out, not_265_out, not_266_out,
       not_267_out, not_268_out, not_269_out, not_270_out, not_271_out, not_272_out, not_273_out,
       not_274_out, not_275_out, not_276_out, not_277_out, not_278_out, not_279_out, not_280_out,
       not_281_out, not_282_out, not_283_out, not_284_out;

  not not_1 (not_1_out, F14);
  not not_2 (not_2_out, F12);
  not not_3 (not_3_out, OP6);
  not not_4 (not_4_out, OP5);
  not not_5 (not_5_out, OP4);
  not not_6 (not_6_out, OP3);
  not not_7 (not_7_out, OP2);
  not not_8 (not_8_out, F14);
  not not_9 (not_9_out, F12);
  not not_10 (not_10_out, OP6);
  not not_11 (not_11_out, OP4);
  not not_12 (not_12_out, OP3);
  not not_13 (not_13_out, OP2);
  not not_14 (not_14_out, F14);
  not not_15 (not_15_out, F13);
  not not_16 (not_16_out, OP6);
  not not_17 (not_17_out, OP4);
  not not_18 (not_18_out, OP3);
  not not_19 (not_19_out, OP2);
  not not_20 (not_20_out, F14);
  not not_21 (not_21_out, F13);
  not not_22 (not_22_out, F12);
  not not_23 (not_23_out, OP6);
  not not_24 (not_24_out, OP5);
  not not_25 (not_25_out, OP3);
  not not_26 (not_26_out, OP2);
  not not_27 (not_27_out, OP6);
  not not_28 (not_28_out, OP5);
  not not_29 (not_29_out, OP3);
  not not_30 (not_30_out, OP2);
  not not_31 (not_31_out, F12);
  not not_32 (not_32_out, OP6);
  not not_33 (not_33_out, OP5);
  not not_34 (not_34_out, OP3);
  not not_35 (not_35_out, OP2);
  not not_36 (not_36_out, F13);
  not not_37 (not_37_out, F12);
  not not_38 (not_38_out, OP6);
  not not_39 (not_39_out, OP5);
  not not_40 (not_40_out, OP3);
  not not_41 (not_41_out, OP2);
  not not_42 (not_42_out, F14);
  not not_43 (not_43_out, F12);
  not not_44 (not_44_out, OP6);
  not not_45 (not_45_out, OP5);
  not not_46 (not_46_out, OP3);
  not not_47 (not_47_out, OP2);
  not not_48 (not_48_out, F30);
  not not_49 (not_49_out, F25);
  not not_50 (not_50_out, F14);
  not not_51 (not_51_out, F13);
  not not_52 (not_52_out, OP6);
  not not_53 (not_53_out, OP5);
  not not_54 (not_54_out, OP3);
  not not_55 (not_55_out, OP2);
  not not_56 (not_56_out, F30);
  not not_57 (not_57_out, F25);
  not not_58 (not_58_out, F13);
  not not_59 (not_59_out, OP6);
  not not_60 (not_60_out, OP5);
  not not_61 (not_61_out, OP3);
  not not_62 (not_62_out, OP2);
  not not_63 (not_63_out, F25);
  not not_64 (not_64_out, F13);
  not not_65 (not_65_out, OP6);
  not not_66 (not_66_out, OP5);
  not not_67 (not_67_out, OP3);
  not not_68 (not_68_out, OP2);
  not not_69 (not_69_out, F14);
  not not_70 (not_70_out, F12);
  not not_71 (not_71_out, OP6);
  not not_72 (not_72_out, OP5);
  not not_73 (not_73_out, OP4);
  not not_74 (not_74_out, OP3);
  not not_75 (not_75_out, OP2);
  not not_76 (not_76_out, F14);
  not not_77 (not_77_out, F12);
  not not_78 (not_78_out, OP6);
  not not_79 (not_79_out, OP4);
  not not_80 (not_80_out, OP3);
  not not_81 (not_81_out, OP2);
  not not_82 (not_82_out, F14);
  not not_83 (not_83_out, F13);
  not not_84 (not_84_out, F12);
  not not_85 (not_85_out, OP4);
  not not_86 (not_86_out, OP3);
  not not_87 (not_87_out, F14);
  not not_88 (not_88_out, F13);
  not not_89 (not_89_out, OP6);
  not not_90 (not_90_out, OP4);
  not not_91 (not_91_out, OP3);
  not not_92 (not_92_out, OP2);
  not not_93 (not_93_out, F14);
  not not_94 (not_94_out, F13);
  not not_95 (not_95_out, F12);
  not not_96 (not_96_out, OP4);
  not not_97 (not_97_out, OP3);
  not not_98 (not_98_out, OP2);
  not not_99 (not_99_out, F14);
  not not_100 (not_100_out, F13);
  not not_101 (not_101_out, OP4);
  not not_102 (not_102_out, OP3);
  not not_103 (not_103_out, OP2);
  not not_104 (not_104_out, F13);
  not not_105 (not_105_out, OP4);
  not not_106 (not_106_out, OP3);
  not not_107 (not_107_out, OP2);
  not not_108 (not_108_out, F30);
  not not_109 (not_109_out, F25);
  not not_110 (not_110_out, F14);
  not not_111 (not_111_out, F13);
  not not_112 (not_112_out, OP6);
  not not_113 (not_113_out, OP5);
  not not_114 (not_114_out, OP3);
  not not_115 (not_115_out, OP2);
  not not_116 (not_116_out, F30);
  not not_117 (not_117_out, F25);
  not not_118 (not_118_out, F13);
  not not_119 (not_119_out, OP6);
  not not_120 (not_120_out, OP5);
  not not_121 (not_121_out, OP3);
  not not_122 (not_122_out, OP2);
  not not_123 (not_123_out, F25);
  not not_124 (not_124_out, F13);
  not not_125 (not_125_out, OP6);
  not not_126 (not_126_out, OP5);
  not not_127 (not_127_out, OP3);
  not not_128 (not_128_out, OP2);
  not not_129 (not_129_out, F13);
  not not_130 (not_130_out, OP4);
  not not_131 (not_131_out, OP3);
  not not_132 (not_132_out, OP2);
  not not_133 (not_133_out, OP6);
  not not_134 (not_134_out, OP3);
  not not_135 (not_135_out, F30);
  not not_136 (not_136_out, F25);
  not not_137 (not_137_out, F14);
  not not_138 (not_138_out, F13);
  not not_139 (not_139_out, F12);
  not not_140 (not_140_out, OP6);
  not not_141 (not_141_out, OP3);
  not not_142 (not_142_out, OP2);
  not not_143 (not_143_out, F25);
  not not_144 (not_144_out, F14);
  not not_145 (not_145_out, F13);
  not not_146 (not_146_out, F12);
  not not_147 (not_147_out, OP6);
  not not_148 (not_148_out, OP3);
  not not_149 (not_149_out, OP2);
  not not_150 (not_150_out, F30);
  not not_151 (not_151_out, F25);
  not not_152 (not_152_out, OP6);
  not not_153 (not_153_out, OP3);
  not not_154 (not_154_out, OP2);
  not not_155 (not_155_out, F30);
  not not_156 (not_156_out, F25);
  not not_157 (not_157_out, F12);
  not not_158 (not_158_out, OP6);
  not not_159 (not_159_out, OP3);
  not not_160 (not_160_out, OP2);
  not not_161 (not_161_out, F30);
  not not_162 (not_162_out, F25);
  not not_163 (not_163_out, F14);
  not not_164 (not_164_out, F12);
  not not_165 (not_165_out, OP6);
  not not_166 (not_166_out, OP3);
  not not_167 (not_167_out, OP2);
  not not_168 (not_168_out, F30);
  not not_169 (not_169_out, F25);
  not not_170 (not_170_out, F14);
  not not_171 (not_171_out, OP6);
  not not_172 (not_172_out, OP3);
  not not_173 (not_173_out, OP2);
  not not_174 (not_174_out, F14);
  not not_175 (not_175_out, F13);
  not not_176 (not_176_out, F12);
  not not_177 (not_177_out, OP6);
  not not_178 (not_178_out, OP5);
  not not_179 (not_179_out, OP3);
  not not_180 (not_180_out, OP2);
  not not_181 (not_181_out, OP6);
  not not_182 (not_182_out, OP5);
  not not_183 (not_183_out, OP3);
  not not_184 (not_184_out, OP2);
  not not_185 (not_185_out, F12);
  not not_186 (not_186_out, OP6);
  not not_187 (not_187_out, OP5);
  not not_188 (not_188_out, OP3);
  not not_189 (not_189_out, OP2);
  not not_190 (not_190_out, F13);
  not not_191 (not_191_out, F12);
  not not_192 (not_192_out, OP6);
  not not_193 (not_193_out, OP5);
  not not_194 (not_194_out, OP3);
  not not_195 (not_195_out, OP2);
  not not_196 (not_196_out, F14);
  not not_197 (not_197_out, F12);
  not not_198 (not_198_out, OP6);
  not not_199 (not_199_out, OP5);
  not not_200 (not_200_out, OP3);
  not not_201 (not_201_out, OP2);
  not not_202 (not_202_out, F30);
  not not_203 (not_203_out, F25);
  not not_204 (not_204_out, F14);
  not not_205 (not_205_out, F13);
  not not_206 (not_206_out, OP6);
  not not_207 (not_207_out, OP5);
  not not_208 (not_208_out, OP3);
  not not_209 (not_209_out, OP2);
  not not_210 (not_210_out, F30);
  not not_211 (not_211_out, F25);
  not not_212 (not_212_out, F13);
  not not_213 (not_213_out, OP6);
  not not_214 (not_214_out, OP5);
  not not_215 (not_215_out, OP3);
  not not_216 (not_216_out, OP2);
  not not_217 (not_217_out, F25);
  not not_218 (not_218_out, F13);
  not not_219 (not_219_out, OP6);
  not not_220 (not_220_out, OP5);
  not not_221 (not_221_out, OP3);
  not not_222 (not_222_out, OP2);
  not not_223 (not_223_out, F14);
  not not_224 (not_224_out, F12);
  not not_225 (not_225_out, OP6);
  not not_226 (not_226_out, OP5);
  not not_227 (not_227_out, OP4);
  not not_228 (not_228_out, OP3);
  not not_229 (not_229_out, OP2);
  not not_230 (not_230_out, OP4);
  not not_231 (not_231_out, F14);
  not not_232 (not_232_out, F13);
  not not_233 (not_233_out, F12);
  not not_234 (not_234_out, OP4);
  not not_235 (not_235_out, OP3);
  not not_236 (not_236_out, F25);
  not not_237 (not_237_out, F13);
  not not_238 (not_238_out, OP6);
  not not_239 (not_239_out, OP3);
  not not_240 (not_240_out, OP2);
  not not_241 (not_241_out, OP6);
  not not_242 (not_242_out, OP3);
  not not_243 (not_243_out, F30);
  not not_244 (not_244_out, F25);
  not not_245 (not_245_out, F14);
  not not_246 (not_246_out, F13);
  not not_247 (not_247_out, F12);
  not not_248 (not_248_out, OP3);
  not not_249 (not_249_out, OP2);
  not not_250 (not_250_out, F14);
  not not_251 (not_251_out, F12);
  not not_252 (not_252_out, OP6);
  not not_253 (not_253_out, OP4);
  not not_254 (not_254_out, OP3);
  not not_255 (not_255_out, OP2);
  not not_256 (not_256_out, F14);
  not not_257 (not_257_out, F13);
  not not_258 (not_258_out, OP6);
  not not_259 (not_259_out, OP4);
  not not_260 (not_260_out, OP3);
  not not_261 (not_261_out, OP2);
  not not_262 (not_262_out, F14);
  not not_263 (not_263_out, F13);
  not not_264 (not_264_out, F12);
  not not_265 (not_265_out, OP4);
  not not_266 (not_266_out, OP3);
  not not_267 (not_267_out, OP2);
  not not_268 (not_268_out, F14);
  not not_269 (not_269_out, F13);
  not not_270 (not_270_out, OP4);
  not not_271 (not_271_out, OP3);
  not not_272 (not_272_out, OP2);
  not not_273 (not_273_out, F14);
  not not_274 (not_274_out, F13);
  not not_275 (not_275_out, F12);
  not not_276 (not_276_out, OP4);
  not not_277 (not_277_out, OP3);
  not not_278 (not_278_out, OP4);
  not not_279 (not_279_out, F14);
  not not_280 (not_280_out, F13);
  not not_281 (not_281_out, OP6);
  not not_282 (not_282_out, OP4);
  not not_283 (not_283_out, OP3);
  not not_284 (not_284_out, OP2);
  and and_1 (MemToReg, not_1_out, F13, not_2_out, not_3_out, not_4_out, not_5_out, not_6_out, not_7_out);
  and and_2 (and_2_out, not_8_out, F13, not_9_out, not_10_out, OP5, not_11_out, not_12_out, not_13_out);
  and and_3 (and_3_out, not_14_out, not_15_out, F12, not_16_out, OP5, not_17_out, not_18_out, not_19_out);
  and and_4 (and_4_out, not_20_out, not_21_out, not_22_out, not_23_out, not_24_out, OP4, not_25_out, not_26_out);
  and and_5 (and_5_out, F14, F13, F12, not_27_out, not_28_out, OP4, not_29_out, not_30_out);
  and and_6 (and_6_out, F14, F13, not_31_out, not_32_out, not_33_out, OP4, not_34_out, not_35_out);
  and and_7 (and_7_out, F14, not_36_out, not_37_out, not_38_out, not_39_out, OP4, not_40_out, not_41_out);
  and and_8 (and_8_out, not_42_out, F13, not_43_out, not_44_out, not_45_out, OP4, not_46_out, not_47_out);
  and and_9 (and_9_out, not_48_out, not_49_out, not_50_out, not_51_out, F12, not_52_out, not_53_out, OP4, not_54_out, not_55_out);
  and and_10 (and_10_out, not_56_out, not_57_out, F14, not_58_out, F12, not_59_out, not_60_out, OP4, not_61_out, not_62_out);
  and and_11 (and_11_out, F30, not_63_out, F14, not_64_out, F12, not_65_out, not_66_out, OP4, not_67_out, not_68_out);
  and and_12 (and_12_out, not_69_out, F13, not_70_out, not_71_out, not_72_out, not_73_out, not_74_out, not_75_out);
  and and_13 (and_13_out, not_76_out, F13, not_77_out, not_78_out, OP5, not_79_out, not_80_out, not_81_out);
  and and_14 (and_14_out, not_82_out, not_83_out, not_84_out, OP6, OP5, not_85_out, not_86_out, OP2);
  and and_15 (and_15_out, not_87_out, not_88_out, F12, not_89_out, OP5, not_90_out, not_91_out, not_92_out);
  and and_16 (and_16_out, not_93_out, not_94_out, not_95_out, OP6, OP5, not_96_out, not_97_out, not_98_out);
  and and_17 (and_17_out, not_99_out, not_100_out, F12, OP6, OP5, not_101_out, not_102_out, not_103_out);
  and and_18 (and_18_out, F14, not_104_out, F12, OP6, OP5, not_105_out, not_106_out, not_107_out);
  and and_19 (and_19_out, not_108_out, not_109_out, not_110_out, not_111_out, F12, not_112_out, not_113_out, OP4, not_114_out, not_115_out);
  and and_20 (and_20_out, not_116_out, not_117_out, F14, not_118_out, F12, not_119_out, not_120_out, OP4, not_121_out, not_122_out);
  and and_21 (and_21_out, F30, not_123_out, F14, not_124_out, F12, not_125_out, not_126_out, OP4, not_127_out, not_128_out);
  and and_22 (bge, F14, not_129_out, F12, OP6, OP5, not_130_out, not_131_out, not_132_out);
  and and_23 (lui, not_133_out, OP5, OP4, not_134_out, OP2);
  and and_24 (and_24_out, not_135_out, not_136_out, not_137_out, not_138_out, not_139_out, not_140_out, OP5, OP4, not_141_out, not_142_out);
  and and_25 (and_25_out, F30, not_143_out, not_144_out, not_145_out, not_146_out, not_147_out, OP5, OP4, not_148_out, not_149_out);
  and and_26 (and_26_out, not_150_out, not_151_out, F14, F13, F12, not_152_out, OP5, OP4, not_153_out, not_154_out);
  and and_27 (and_27_out, not_155_out, not_156_out, F14, F13, not_157_out, not_158_out, OP5, OP4, not_159_out, not_160_out);
  and and_28 (and_28_out, not_161_out, not_162_out, not_163_out, F13, not_164_out, not_165_out, OP5, OP4, not_166_out, not_167_out);
  and and_29 (and_29_out, not_168_out, not_169_out, not_170_out, F13, F12, not_171_out, OP5, OP4, not_172_out, not_173_out);
  and and_30 (and_30_out, not_174_out, not_175_out, not_176_out, not_177_out, not_178_out, OP4, not_179_out, not_180_out);
  and and_31 (and_31_out, F14, F13, F12, not_181_out, not_182_out, OP4, not_183_out, not_184_out);
  and and_32 (and_32_out, F14, F13, not_185_out, not_186_out, not_187_out, OP4, not_188_out, not_189_out);
  and and_33 (and_33_out, F14, not_190_out, not_191_out, not_192_out, not_193_out, OP4, not_194_out, not_195_out);
  and and_34 (and_34_out, not_196_out, F13, not_197_out, not_198_out, not_199_out, OP4, not_200_out, not_201_out);
  and and_35 (and_35_out, not_202_out, not_203_out, not_204_out, not_205_out, F12, not_206_out, not_207_out, OP4, not_208_out, not_209_out);
  and and_36 (and_36_out, not_210_out, not_211_out, F14, not_212_out, F12, not_213_out, not_214_out, OP4, not_215_out, not_216_out);
  and and_37 (and_37_out, F30, not_217_out, F14, not_218_out, F12, not_219_out, not_220_out, OP4, not_221_out, not_222_out);
  and and_38 (and_38_out, not_223_out, F13, not_224_out, not_225_out, not_226_out, not_227_out, not_228_out, not_229_out);
  and and_39 (and_39_out, OP6, OP5, not_230_out, OP3, OP2);
  and and_40 (and_40_out, not_231_out, not_232_out, not_233_out, OP6, OP5, not_234_out, not_235_out, OP2);
  and and_41 (and_41_out, F30, not_236_out, F14, not_237_out, F12, not_238_out, OP5, OP4, not_239_out, not_240_out);
  and and_42 (and_42_out, not_241_out, OP5, OP4, not_242_out, OP2);
  and and_43 (ecall, not_243_out, not_244_out, not_245_out, not_246_out, not_247_out, OP6, OP5, OP4, not_248_out, not_249_out);
  and and_44 (and_44_out, not_250_out, F13, not_251_out, not_252_out, OP5, not_253_out, not_254_out, not_255_out);
  and and_45 (and_45_out, not_256_out, not_257_out, F12, not_258_out, OP5, not_259_out, not_260_out, not_261_out);
  and and_46 (BEQ, not_262_out, not_263_out, not_264_out, OP6, OP5, not_265_out, not_266_out, not_267_out);
  and and_47 (BNE, not_268_out, not_269_out, F12, OP6, OP5, not_270_out, not_271_out, not_272_out);
  and and_48 (JALR, not_273_out, not_274_out, not_275_out, OP6, OP5, not_276_out, not_277_out, OP2);
  and and_49 (JAL, OP6, OP5, not_278_out, OP3, OP2);
  and and_50 (sh, not_279_out, not_280_out, F12, not_281_out, OP5, not_282_out, not_283_out, not_284_out);
  or or_1 (MemWrite, and_2_out, and_3_out);
  or or_2 (B_Type, and_16_out, and_17_out, and_18_out);
  or or_3 (ShiftImm, and_19_out, and_20_out, and_21_out);
  or or_4 (S_Type, and_44_out, and_45_out);
  or or_5 (ALU_SRC, and_4_out, and_5_out, and_6_out, and_7_out, and_8_out, and_9_out, and_10_out, and_11_out, and_12_out, and_13_out, and_14_out, and_15_out);
  or or_6 (RegWrite, and_24_out, and_25_out, and_26_out, and_27_out, and_28_out, and_29_out, and_30_out, and_31_out, and_32_out, and_33_out, and_34_out, and_35_out, and_36_out, and_37_out, and_38_out, and_39_out, and_40_out, and_41_out, and_42_out);
endmodule

// ALU
module ALU (
  input  [31:0] X,
  input  [31:0] Y,
  input  [3:0] AluOP,
  output out_4,
  output Equal,
  output out_6,
  output [31:0] Result,
  output [31:0] Result_2
);

  wire [0:0] comparator_1_lt, comparator_2_lt;
  wire [31:0] adder_1_out, AND_out, divider_1_out, divider_1_rem, multiplier_1_cout, multiplier_1_out,
       NOR_out, OR_out, shifter_1_out, shifter_2_out, shifter_3_out, subtractor_1_out, XOR_out;

  assign AND_out = X & Y;  // AND_Gate AND, 32 bits wide
  assign OR_out = X | Y;  // OR_Gate OR, 32 bits wide
  Shifter #(.width(32), .shift("ll")) shifter_1 (.in(X), .\dist (Y[4:0]), .out(shifter_1_out));
  Shifter #(.width(32), .shift("ar")) shifter_2 (.in(X), .\dist (Y[4:0]), .out(shifter_2_out));
  Shifter #(.width(32), .shift("lr")) shifter_3 (.in(X), .\dist (Y[4:0]), .out(shifter_3_out));
  Multiplier #(.width(32)) multiplier_1 (.a(X), .b(Y), .out(multiplier_1_out), .cout(multiplier_1_cout));  // open: cin
  Divider #(.width(32)) divider_1 (.a(X), .b(Y), .out(divider_1_out), .rem(divider_1_rem));  // open: upper
  Adder #(.width(32)) adder_1 (.a(X), .b(Y), .out(adder_1_out));  // open: cin, cout
  Subtractor #(.width(32)) subtractor_1 (.a(X), .b(Y), .out(subtractor_1_out));  // open: bin, bout
  assign XOR_out = X ^ Y;  // XOR_Gate XOR, 32 bits wide
  assign NOR_out = ~(X | Y);  // NOR_Gate NOR, 32 bits wide
  Comparator #(.width(32), .mode("twosComplement")) comparator_1 (
    .a(X), .b(Y), .eq(Equal), .lt(comparator_1_lt[0]));  // open: gt
  Comparator #(.width(32), .mode("unsigned")) comparator_2 (.a(X), .b(Y), .lt(comparator_2_lt[0]));  // open: gt, eq
  Multiplexer #(.select(4), .width(32), .disabled("Z"), .enable("false")) multiplexer_1 (
    .in0(shifter_1_out), .in1(shifter_2_out), .in2(shifter_3_out), .in3(multiplier_1_out),
    .in4(divider_1_out), .in5(adder_1_out), .in6(subtractor_1_out), .in7(AND_out), .in8(OR_out),
    .in9(XOR_out), .in10(NOR_out), .in11({{31{1'b0}}, comparator_1_lt[0]}),
    .in12({{31{1'b0}}, comparator_2_lt[0]}), .in13({32{1'b0}}), .in14({32{1'b0}}), .in15({32{1'b0}}),
    .out(Result), .sel(AluOP));
  Multiplexer #(.select(4), .width(32), .disabled("Z"), .enable("false")) multiplexer_2 (
    .in0({32{1'b0}}), .in1({32{1'b0}}), .in2({32{1'b0}}), .in3(multiplier_1_cout), .in4(divider_1_rem),
    .in5({32{1'b0}}), .in6({32{1'b0}}), .in7({32{1'b0}}), .in8({32{1'b0}}), .in9({32{1'b0}}),
    .in10({32{1'b0}}), .in11({32{1'b0}}), .in12({32{1'b0}}), .in13({32{1'b0}}), .in14({32{1'b0}}),
    .in15({32{1'b0}}), .out(Result_2), .sel(AluOP));
  Multiplexer #(.select(4), .width(1), .disabled("Z"), .enable("false")) multiplexer_3 (
    .in0(1'b0), .in1(1'b0), .in2(1'b0), .in3(1'b0), .in4(1'b0), .in5(1'b0), .in6(1'b0), .in7(1'b0),
    .in8(1'b0), .in9(1'b0), .in10(1'b0), .in11(comparator_1_lt[0]), .in12(comparator_2_lt[0]), .in13(1'b0),
    .in14(1'b0), .in15(1'b0), .out(out_6), .sel(AluOP));
  not not_1 (out_4, out_6);

  // Other names for the same wires on the sheet: Result2[31:0] = Result_2; S[3:0] = AluOP; tunnel = out_6;
  //   tunnel_t = out_4

  // Notes on the sheet:
  //   不要改变此引脚区域内容，也不要改变ALU封装形式
  //   输入引脚
  //   输出引脚
endmodule

module Regifile (
  input  [31:0] Din,
  input  Clk,
  input  WE,
  input  [4:0] R1_num,
  input  [4:0] W_num,
  input  [4:0] R2_num,
  output [31:0] R1,
  output [31:0] R2
);

  // RegisterFile registerfile_1: pin names not known; wires that end beside it: Din, Clk, WE, W_num, R1_num, R2_num, R1, R2
endmodule

module \中断按键参考电路  (
  input  \同步清零信号 ,
  output \与中断屏蔽位与 
);

  wire \_1号中断_out , and_1_out, clock_1_out, d_ff_1_q, or_1_out, or_2_out;

  Clock #(.highDuration(1), .lowDuration(1)) clock_1 (.out(clock_1_out));
  Button \_1号中断  (.out(\_1号中断_out ));
  LED #(.active("true")) \_1号中断等待指示灯  (.in(or_1_out));
  or or_1 (or_1_out, \与中断屏蔽位与 , d_ff_1_q);
  D_Flip_Flop #(.trigger("rising"), .Pre_Clr_Positions("LEGACY"), .NegatePresetClear("false"), .enable("true"), .NewFFLayout("false")) d_ff_1 (
    .clk(\_1号中断_out ), .D(1'b1), .Q(d_ff_1_q), .reset(\与中断屏蔽位与 ));  // open: Qn, preset, en
  or or_2 (or_2_out, d_ff_1_q, \与中断屏蔽位与 );
  and and_1 (and_1_out, or_2_out, ~\同步清零信号 );  // AND_Gate
  D_Flip_Flop #(.trigger("rising"), .Pre_Clr_Positions("LEGACY"), .NegatePresetClear("false"), .enable("true"), .NewFFLayout("false")) IR1 (
    .clk(clock_1_out), .D(and_1_out), .Q(\与中断屏蔽位与 ));  // open: Qn, preset, en, reset

  // Notes on the sheet:
  //   中断信号采样参考电路
  //   Reset 
endmodule

module \单周期_单级中断  (
  input  IR1,
  input  IR2,
  input  IR3,
  output RegWrite,
  output MemWrite,
  output [31:0] PC,
  output [31:0] IR,
  output [31:0] RDin,
  output [31:0] MDin,
  output [31:0] LedData
);

  wire CLK, clock_1_out, comparator_1_eq, comparator_2_eq, comparator_3_eq, comparator_4_eq, comparator_5_eq,
       comparator_5_lt, d_ff_1_q, Go, IR1_t, IR2_t, IR3_t, IRA, IRB, IRC, nand_1_out, or_1_out, W1, W2, W3;
  wire [12:0] CNT_num;
  wire [15:0] \总周期数 ;

  Button \u_继续运行  (.out(Go));
  Button _1 ();  // open: out
  Button _2 ();  // open: out
  Button _3 ();  // open: out
  LED #(.active("true")) led_1 (.in(W1));
  LED #(.active("true")) led_2 (.in(W2));
  LED #(.active("true")) led_3 (.in(W3));
  Hex_Digit_Display hex_digit_display_1 (.value(LedData[31:28]));  // open: dp
  Comparator #(.width(16), .mode("twosComplement")) comparator_1 (
    .a(16'h23b), .b(\总周期数 ), .eq(comparator_1_eq));  // open: gt, lt
  Comparator #(.width(16), .mode("twosComplement")) comparator_2 (
    .a(\总周期数 ), .b(16'h1), .eq(comparator_2_eq));  // open: gt, lt
  Comparator #(.width(16), .mode("twosComplement")) comparator_3 (
    .a(\总周期数 ), .b(16'h4), .eq(comparator_3_eq));  // open: gt, lt
  Comparator #(.width(16), .mode("twosComplement")) comparator_4 (
    .a(\总周期数 ), .b(16'h7), .eq(comparator_4_eq));  // open: gt, lt
  Hex_Digit_Display hex_digit_display_2 (.value(LedData[23:20]));  // open: dp
  Hex_Digit_Display hex_digit_display_3 (.value(LedData[27:24]));  // open: dp
  or or_1 (or_1_out, comparator_1_eq, comparator_2_eq);
  assign IRA = or_1_out ? ~CLK : 1'bz;  // Controlled_Inverter controlled_inverter_1
  assign IRB = comparator_3_eq ? ~CLK : 1'bz;  // Controlled_Inverter controlled_inverter_2
  assign IRC = comparator_4_eq ? ~CLK : 1'bz;  // Controlled_Inverter controlled_inverter_3
  Hex_Digit_Display hex_digit_display_4 (.value(LedData[15:12]));  // open: dp
  Hex_Digit_Display hex_digit_display_5 (.value(LedData[19:16]));  // open: dp
  Pull_Resistor #(.pull(0)) pull_resistor_1 (.node(IRA));
  Pull_Resistor #(.pull(0)) pull_resistor_2 (.node(IRB));
  Pull_Resistor #(.pull(0)) pull_resistor_3 (.node(IRC));
  Hex_Digit_Display hex_digit_display_6 (.value(LedData[11:8]));  // open: dp
  Hex_Digit_Display hex_digit_display_7 (.value(LedData[7:4]));  // open: dp
  // Probe on \总周期数 
  Hex_Digit_Display hex_digit_display_8 (.value(LedData[3:0]));  // open: dp
  or or_2 (IR1_t, IR1, IRA);
  or or_3 (IR2_t, IR2, IRB);
  or or_4 (IR3_t, IR3, IRC);
  D_Flip_Flop #(.trigger("high"), .Pre_Clr_Positions("LEGACY"), .NegatePresetClear("false"), .enable("true"), .NewFFLayout("false")) d_ff_1 (.Q(d_ff_1_q));  // open: clk, D, Qn, preset, en, reset
  // Probe on 13'hc
  Comparator #(.width(13), .mode("twosComplement")) comparator_5 (
    .a(CNT_num), .b(13'hc), .eq(comparator_5_eq), .lt(comparator_5_lt));  // open: gt
  Clock #(.highDuration(1), .lowDuration(1)) clock_1 (.out(clock_1_out));
  Counter #(.width(13), .max('h1fff), .ongoal("stay"), .trigger("rising"), .behavior("old")) counter_1 (
    .count(comparator_5_lt), .Q(CNT_num), .clk(clock_1_out));  // open: load, D, carry, clr, preset
  nand nand_1 (nand_1_out, d_ff_1_q, comparator_5_eq);
  assign CLK = nand_1_out ? clock_1_out : 1'bz;  // Controlled_Buffer controlled_buffer_1
  Pull_Resistor #(.pull(1)) pull_resistor_4 (.node(CLK));

  // Notes on the sheet:
  //   中断源
  //   中断等待指示
  //   总复位信号应将除ROM以外所有存储组件全部清零
  //   单级中断测试信号模拟器
  //   数码管输出
  //   数码管输出应该用寄存器锁存，否则显示数据只能一闪而过
  //   为方便自动评测，需要输出PC，IR，寄存器堆写如数据RDin
  //   RAM写使能MemWrite、RAM写入数据MDin等信号
  //   控制位
  //   暂停节拍，不能为0
  //   戳工具置1进入计数暂停模式，ctrl+k时钟自动运行到对应节拍暂停
  //   ctrl+k关闭时钟连续运行，将控制位置零，进入单步调试模式调试
  //   可计数暂停的时钟源
endmodule

module \单周期_多级中断  (
  input  IR1,
  input  IR2,
  input  IR3,
  output RegWrite,
  output MemWrite,
  output [31:0] PC,
  output [31:0] IR,
  output [31:0] RDin,
  output [31:0] MDin,
  output [31:0] LedData
);

  wire CLK, clock_1_out, comparator_1_eq, comparator_2_eq, comparator_3_eq, comparator_4_eq, comparator_5_eq,
       comparator_6_eq, comparator_6_lt, d_ff_1_q, Go, IR1_t, IR2_t, IR3_t, IRA, IRB, IRC, nand_1_out,
       or_1_out, or_2_out, W1, W2, W3;
  wire [12:0] CNT_num;
  wire [15:0] \总周期数 ;

  Button \u_继续运行  (.out(Go));
  Button _1 ();  // open: out
  Button _2 ();  // open: out
  Button _3 ();  // open: out
  LED #(.active("true")) led_1 (.in(W1));
  LED #(.active("true")) led_2 (.in(W2));
  LED #(.active("true")) led_3 (.in(W3));
  Hex_Digit_Display hex_digit_display_1 (.value(LedData[31:28]));  // open: dp
  Comparator #(.width(16), .mode("twosComplement")) comparator_1 (
    .a(\总周期数 ), .b(16'h7), .eq(comparator_1_eq));  // open: gt, lt
  Comparator #(.width(16), .mode("twosComplement")) comparator_2 (
    .a(\总周期数 ), .b(16'h241), .eq(comparator_2_eq));  // open: gt, lt
  Hex_Digit_Display hex_digit_display_2 (.value(LedData[23:20]));  // open: dp
  Hex_Digit_Display hex_digit_display_3 (.value(LedData[27:24]));  // open: dp
  Comparator #(.width(16), .mode("twosComplement")) comparator_3 (
    .a(16'h258), .b(\总周期数 ), .eq(comparator_3_eq));  // open: gt, lt
  or or_1 (or_1_out, comparator_3_eq, comparator_4_eq);
  Comparator #(.width(16), .mode("twosComplement")) comparator_4 (
    .a(\总周期数 ), .b(16'h1), .eq(comparator_4_eq));  // open: gt, lt
  Comparator #(.width(16), .mode("twosComplement")) comparator_5 (
    .a(\总周期数 ), .b(16'h4), .eq(comparator_5_eq));  // open: gt, lt
  or or_2 (or_2_out, comparator_1_eq, comparator_2_eq);
  Hex_Digit_Display hex_digit_display_4 (.value(LedData[19:16]));  // open: dp
  Hex_Digit_Display hex_digit_display_5 (.value(LedData[15:12]));  // open: dp
  Pull_Resistor #(.pull(0)) pull_resistor_1 (.node(IRA));
  assign IRA = or_1_out ? ~CLK : 1'bz;  // Controlled_Inverter controlled_inverter_1
  Pull_Resistor #(.pull(0)) pull_resistor_2 (.node(IRB));
  assign IRB = comparator_5_eq ? ~CLK : 1'bz;  // Controlled_Inverter controlled_inverter_2
  Pull_Resistor #(.pull(0)) pull_resistor_3 (.node(IRC));
  assign IRC = or_2_out ? ~CLK : 1'bz;  // Controlled_Inverter controlled_inverter_3
  Hex_Digit_Display hex_digit_display_6 (.value(LedData[7:4]));  // open: dp
  Hex_Digit_Display hex_digit_display_7 (.value(LedData[11:8]));  // open: dp
  // Probe on \总周期数 
  Hex_Digit_Display hex_digit_display_8 (.value(LedData[3:0]));  // open: dp
  or or_3 (IR1_t, IR1, IRA);
  or or_4 (IR2_t, IR2, IRB);
  or or_5 (IR3_t, IR3, IRC);
  D_Flip_Flop #(.trigger("high"), .Pre_Clr_Positions("LEGACY"), .NegatePresetClear("false"), .enable("true"), .NewFFLayout("false")) d_ff_1 (.Q(d_ff_1_q));  // open: clk, D, Qn, preset, en, reset
  // Probe on 13'hc
  Comparator #(.width(13), .mode("twosComplement")) comparator_6 (
    .a(CNT_num), .b(13'hc), .eq(comparator_6_eq), .lt(comparator_6_lt));  // open: gt
  Clock #(.highDuration(1), .lowDuration(1)) clock_1 (.out(clock_1_out));
  Counter #(.width(13), .max('h1fff), .ongoal("stay"), .trigger("rising"), .behavior("old")) counter_1 (
    .count(comparator_6_lt), .Q(CNT_num), .clk(clock_1_out));  // open: load, D, carry, clr, preset
  nand nand_1 (nand_1_out, d_ff_1_q, comparator_6_eq);
  assign CLK = nand_1_out ? clock_1_out : 1'bz;  // Controlled_Buffer controlled_buffer_1
  Pull_Resistor #(.pull(1)) pull_resistor_4 (.node(CLK));

  // Notes on the sheet:
  //   中断源
  //   中断等待指示
  //   总复位信号应将除ROM以外所有存储组件全部清零
  //   多级中断测试信号模拟器
  //   数码管输出
  //   数码管输出应该用寄存器锁存，否则显示数据只能一闪而过
  //   为方便自动评测，需要输出PC，IR，寄存器堆写如数据RDin
  //   RAM写使能MemWrite、RAM写入数据MDin等信号
  //   控制位
  //   暂停节拍，不能为0
  //   戳工具置1进入计数暂停模式，ctrl+k时钟自动运行到对应节拍暂停
  //   ctrl+k关闭时钟连续运行，将控制位置零，进入单步调试模式调试
  //   可计数暂停的时钟源
endmodule

module \封装正确性测试  (
);

  wire IR1, IR2, IR3, MemW, RegW;
  wire [31:0] EX_PC, ID_PC, IF_PC, IR, LED, MDin, MDinr, MEM_PC, PC, RDin, RDinr, WB_PC;

  \单周期RISC_V  \u_单周期risc_v_1  (
    .IR1(IR1), .IR2(IR2), .IR3(IR3), .RegWrite(RegW), .MemWrite(MemW), .PC(PC), .IR(IR), .RDin(RDin),
    .MDin(MDin), .LedData(LED));
  \气泡流水线  \u_气泡流水线_1  (
    .RegWrite(RegW), .MemWrite(MemW), .IF_PC(IF_PC), .ID_PC(ID_PC), .EX_PC(EX_PC), .M_PC(MEM_PC),
    .WB_PC(WB_PC), .RDin(RDinr), .MDin(MDinr), .LedData(LED));
  \单周期_单级中断  \u_单周期_单级中断_1  (
    .IR1(IR1), .IR2(IR2), .IR3(IR3), .RegWrite(RegW), .MemWrite(MemW), .PC(PC), .IR(IR), .RDin(RDin),
    .MDin(MDin), .LedData(LED));
  \理想流水线  \u_理想流水线_1  (
    .RegWrite(RegW), .MemWrite(MemW), .IF_PC(IF_PC), .ID_PC(ID_PC), .EX_PC(EX_PC), .M_PC(MEM_PC),
    .WB_PC(WB_PC), .RDin(RDinr), .MDin(MDinr), .LedData(LED));
  \重定向流水线  \u_重定向流水线_1  (
    .RegWrite(RegW), .MemWrite(MemW), .IF_PC(IF_PC), .ID_PC(ID_PC), .EX_PC(EX_PC), .M_PC(MEM_PC),
    .WB_PC(WB_PC), .RDin(RDinr), .MDin(MDinr), .LedData(LED));
  \单周期_多级中断  \u_单周期_多级中断_1  (
    .IR1(IR1), .IR2(IR2), .IR3(IR3), .RegWrite(RegW), .MemWrite(MemW), .PC(PC), .IR(IR), .RDin(RDin),
    .MDin(MDin), .LedData(LED));

  // Notes on the sheet:
  //   单周期封装测试
  //   气泡流水封装测试
  //   单周期+单级中断封装测试
  //   请检查上面封装有无位宽不匹配，引脚标签是否和连接的标签相对应，否则无法在educoder平台上正确测试
  //   理想流水封装测试
  //   重定向流水封装测试
  //   单周期+多级中断封装测试
endmodule

module Decoder (
  input  [4:0] OP,
  input  [2:0] Funct3,
  input  [6:0] Funct7,
  output B,
  output ShiftImm
);

  wire comparator_2_eq, comparator_3_eq, comparator_4_eq, or_1_out;

  Comparator #(.width(5), .mode("twosComplement")) comparator_1 (.a(OP), .b(5'b11000), .eq(B));  // open: gt, lt
  Comparator #(.width(5), .mode("twosComplement")) comparator_2 (
    .a(OP), .b(5'b00100), .eq(comparator_2_eq));  // open: gt, lt
  Comparator #(.width(3), .mode("twosComplement")) comparator_3 (
    .a(Funct3), .b(3'b001), .eq(comparator_3_eq));  // open: gt, lt
  Comparator #(.width(3), .mode("twosComplement")) comparator_4 (
    .a(Funct3), .b(3'b101), .eq(comparator_4_eq));  // open: gt, lt
  or or_1 (or_1_out, comparator_3_eq, comparator_4_eq);
  and and_1 (ShiftImm, comparator_2_eq, or_1_out);
endmodule

module IF_ID (
  input  [31:0] IRin,
  input  [31:0] PCin,
  input  CLK,
  input  clear,
  input  Stall,
  input  halt,
  output [31:0] IRout,
  output [31:0] PCout
);

  wire and_1_out, not_1_out, not_2_out;
  wire [31:0] multiplexer_1_out, multiplexer_2_out;

  not not_1 (not_1_out, Stall);
  not not_2 (not_2_out, halt);
  and and_1 (and_1_out, not_1_out, not_2_out);
  Multiplexer #(.select(1), .width(32), .disabled("Z"), .enable("false")) multiplexer_1 (
    .in0(IRin), .in1({32{1'b0}}), .out(multiplexer_1_out), .sel(clear));
  Multiplexer #(.select(1), .width(32), .disabled("Z"), .enable("false")) multiplexer_2 (
    .in0(PCin), .in1({32{1'b0}}), .out(multiplexer_2_out), .sel(clear));
  Register #(.width(32), .trigger("rising"), .Select("low")) register_1 (
    .D(multiplexer_1_out), .en(and_1_out), .Q(IRout), .clk(CLK));  // open: clr
  Register #(.width(32), .trigger("rising"), .Select("low")) register_2 (
    .D(multiplexer_2_out), .en(and_1_out), .Q(PCout), .clk(CLK));  // open: clr
endmodule

module ID_EX (
  input  [31:0] IRin,
  input  [31:0] PCin,
  input  [31:0] RS1in,
  input  [31:0] RS2in,
  input  [31:0] Imm_in,
  input  RegWrite_in,
  input  MemWrite_in,
  input  [4:0] RegWriteNum_in,
  input  ALU_src_in,
  input  jal_in,
  input  jalr_in,
  input  beq_in,
  input  bne_in,
  input  bge_in,
  input  sh_in,
  input  lui_in,
  input  ecall_in,
  input  Mem2Reg_in,
  input  [31:0] BImm_in,
  input  [31:0] UImm_in,
  input  [31:0] JImm_in,
  input  [3:0] ALI_op_in,
  input  CLK,
  input  halt,
  input  clear,
  output [31:0] IRout,
  output [31:0] PCout,
  output [31:0] RS1out,
  output [31:0] RS2out,
  output [31:0] Imm_out,
  output RegWrite_out,
  output MemWrite_out,
  output [4:0] RegWriteNum_out,
  output ALU_src_out,
  output jal_out,
  output jalr_out,
  output beq_out,
  output bne_out,
  output bge_out,
  output sh_out,
  output lui_out,
  output ecall_out,
  output Mem2Reg_out,
  output [31:0] BImm_out,
  output [31:0] UImm_out,
  output [31:0] JImm_out,
  output [3:0] ALU_op_out
);

  wire multiplexer_1_out, multiplexer_2_out, multiplexer_3_out, multiplexer_4_out, multiplexer_10_out,
       multiplexer_11_out, multiplexer_13_out, multiplexer_14_out, multiplexer_15_out, multiplexer_16_out,
       multiplexer_17_out, multiplexer_18_out, not_1_out;
  wire [3:0] multiplexer_22_out;
  wire [4:0] multiplexer_12_out;
  wire [31:0] multiplexer_5_out, multiplexer_6_out, multiplexer_7_out, multiplexer_8_out, multiplexer_9_out,
       multiplexer_19_out, multiplexer_20_out, multiplexer_21_out;

  Multiplexer #(.select(1), .width(1), .disabled("Z"), .enable("false")) multiplexer_1 (
    .in0(ALU_src_in), .in1(1'b0), .out(multiplexer_1_out), .sel(clear));
  Multiplexer #(.select(1), .width(1), .disabled("Z"), .enable("false")) multiplexer_2 (
    .in0(beq_in), .in1(1'b0), .out(multiplexer_2_out), .sel(clear));
  Multiplexer #(.select(1), .width(1), .disabled("Z"), .enable("false")) multiplexer_3 (
    .in0(bne_in), .in1(1'b0), .out(multiplexer_3_out), .sel(clear));
  Multiplexer #(.select(1), .width(1), .disabled("Z"), .enable("false")) multiplexer_4 (
    .in0(bge_in), .in1(1'b0), .out(multiplexer_4_out), .sel(clear));
  Multiplexer #(.select(1), .width(32), .disabled("Z"), .enable("false")) multiplexer_5 (
    .in0(IRin), .in1({32{1'b0}}), .out(multiplexer_5_out), .sel(clear));
  Multiplexer #(.select(1), .width(32), .disabled("Z"), .enable("false")) multiplexer_6 (
    .in0(PCin), .in1({32{1'b0}}), .out(multiplexer_6_out), .sel(clear));
  Multiplexer #(.select(1), .width(32), .disabled("Z"), .enable("false")) multiplexer_7 (
    .in0(RS1in), .in1({32{1'b0}}), .out(multiplexer_7_out), .sel(clear));
  Multiplexer #(.select(1), .width(32), .disabled("Z"), .enable("false")) multiplexer_8 (
    .in0(RS2in), .in1({32{1'b0}}), .out(multiplexer_8_out), .sel(clear));
  Multiplexer #(.select(1), .width(32), .disabled("Z"), .enable("false")) multiplexer_9 (
    .in0(Imm_in), .in1({32{1'b0}}), .out(multiplexer_9_out), .sel(clear));
  Multiplexer #(.select(1), .width(1), .disabled("Z"), .enable("false")) multiplexer_10 (
    .in0(RegWrite_in), .in1(1'b0), .out(multiplexer_10_out), .sel(clear));
  Multiplexer #(.select(1), .width(1), .disabled("Z"), .enable("false")) multiplexer_11 (
    .in0(MemWrite_in), .in1(1'b0), .out(multiplexer_11_out), .sel(clear));
  Multiplexer #(.select(1), .width(5), .disabled("Z"), .enable("false")) multiplexer_12 (
    .in0(RegWriteNum_in), .in1({5{1'b0}}), .out(multiplexer_12_out), .sel(clear));
  Multiplexer #(.select(1), .width(1), .disabled("Z"), .enable("false")) multiplexer_13 (
    .in0(jal_in), .in1(1'b0), .out(multiplexer_13_out), .sel(clear));
  Multiplexer #(.select(1), .width(1), .disabled("Z"), .enable("false")) multiplexer_14 (
    .in0(jalr_in), .in1(1'b0), .out(multiplexer_14_out), .sel(clear));
  Multiplexer #(.select(1), .width(1), .disabled("Z"), .enable("false")) multiplexer_15 (
    .in0(sh_in), .in1(1'b0), .out(multiplexer_15_out), .sel(clear));
  Multiplexer #(.select(1), .width(1), .disabled("Z"), .enable("false")) multiplexer_16 (
    .in0(lui_in), .in1(1'b0), .out(multiplexer_16_out), .sel(clear));
  Multiplexer #(.select(1), .width(1), .disabled("Z"), .enable("false")) multiplexer_17 (
    .in0(ecall_in), .in1(1'b0), .out(multiplexer_17_out), .sel(clear));
  Multiplexer #(.select(1), .width(1), .disabled("Z"), .enable("false")) multiplexer_18 (
    .in0(Mem2Reg_in), .in1(1'b0), .out(multiplexer_18_out), .sel(clear));
  Multiplexer #(.select(1), .width(32), .disabled("Z"), .enable("false")) multiplexer_19 (
    .in0(BImm_in), .in1({32{1'b0}}), .out(multiplexer_19_out), .sel(clear));
  Multiplexer #(.select(1), .width(32), .disabled("Z"), .enable("false")) multiplexer_20 (
    .in0(UImm_in), .in1({32{1'b0}}), .out(multiplexer_20_out), .sel(clear));
  Multiplexer #(.select(1), .width(32), .disabled("Z"), .enable("false")) multiplexer_21 (
    .in0(JImm_in), .in1({32{1'b0}}), .out(multiplexer_21_out), .sel(clear));
  Multiplexer #(.select(1), .width(4), .disabled("Z"), .enable("false")) multiplexer_22 (
    .in0(ALI_op_in), .in1(4'b0000), .out(multiplexer_22_out), .sel(clear));
  Register #(.width(32), .trigger("rising"), .Select("low")) register_1 (
    .D(multiplexer_5_out), .en(not_1_out), .Q(IRout), .clk(CLK));  // open: clr
  Register #(.width(32), .trigger("rising"), .Select("low")) register_2 (
    .D(multiplexer_6_out), .en(not_1_out), .Q(PCout), .clk(CLK));  // open: clr
  Register #(.width(32), .trigger("rising"), .Select("low")) register_3 (
    .D(multiplexer_7_out), .en(not_1_out), .Q(RS1out), .clk(CLK));  // open: clr
  Register #(.width(32), .trigger("rising"), .Select("low")) register_4 (
    .D(multiplexer_8_out), .en(not_1_out), .Q(RS2out), .clk(CLK));  // open: clr
  Register #(.width(32), .trigger("rising"), .Select("low")) register_5 (
    .D(multiplexer_9_out), .en(not_1_out), .Q(Imm_out), .clk(CLK));  // open: clr
  Register #(.width(1), .trigger("rising"), .Select("low")) register_6 (
    .D(multiplexer_10_out), .en(not_1_out), .Q(RegWrite_out), .clk(CLK));  // open: clr
  Register #(.width(1), .trigger("rising"), .Select("low")) register_7 (
    .D(multiplexer_11_out), .en(not_1_out), .Q(MemWrite_out), .clk(CLK));  // open: clr
  Register #(.width(5), .trigger("rising"), .Select("low")) register_8 (
    .D(multiplexer_12_out), .en(not_1_out), .Q(RegWriteNum_out), .clk(CLK));  // open: clr
  Register #(.width(1), .trigger("rising"), .Select("low")) register_9 (
    .D(multiplexer_1_out), .en(not_1_out), .Q(ALU_src_out), .clk(CLK));  // open: clr
  Register #(.width(1), .trigger("rising"), .Select("low")) register_10 (
    .D(multiplexer_13_out), .en(not_1_out), .Q(jal_out), .clk(CLK));  // open: clr
  Register #(.width(1), .trigger("rising"), .Select("low")) register_11 (
    .D(multiplexer_14_out), .en(not_1_out), .Q(jalr_out), .clk(CLK));  // open: clr
  Register #(.width(1), .trigger("rising"), .Select("low")) register_12 (
    .D(multiplexer_2_out), .en(not_1_out), .Q(beq_out), .clk(CLK));  // open: clr
  Register #(.width(1), .trigger("rising"), .Select("low")) register_13 (
    .D(multiplexer_3_out), .en(not_1_out), .Q(bne_out), .clk(CLK));  // open: clr
  Register #(.width(1), .trigger("rising"), .Select("low")) register_14 (
    .D(multiplexer_4_out), .en(not_1_out), .Q(bge_out), .clk(CLK));  // open: clr
  Register #(.width(1), .trigger("rising"), .Select("low")) register_15 (
    .D(multiplexer_15_out), .en(not_1_out), .Q(sh_out), .clk(CLK));  // open: clr
  Register #(.width(1), .trigger("rising"), .Select("low")) register_16 (
    .D(multiplexer_16_out), .en(not_1_out), .Q(lui_out), .clk(CLK));  // open: clr
  Register #(.width(1), .trigger("rising"), .Select("low")) register_17 (
    .D(multiplexer_17_out), .en(not_1_out), .Q(ecall_out), .clk(CLK));  // open: clr
  Register #(.width(1), .trigger("rising"), .Select("low")) register_18 (
    .D(multiplexer_18_out), .en(not_1_out), .Q(Mem2Reg_out), .clk(CLK));  // open: clr
  Register #(.width(32), .trigger("rising"), .Select("low")) register_19 (
    .D(multiplexer_19_out), .en(not_1_out), .Q(BImm_out), .clk(CLK));  // open: clr
  Register #(.width(32), .trigger("rising"), .Select("low")) register_20 (
    .D(multiplexer_20_out), .en(not_1_out), .Q(UImm_out), .clk(CLK));  // open: clr
  Register #(.width(32), .trigger("rising"), .Select("low")) register_21 (
    .D(multiplexer_21_out), .en(not_1_out), .Q(JImm_out), .clk(CLK));  // open: clr
  Register #(.width(4), .trigger("rising"), .Select("low")) register_22 (
    .D(multiplexer_22_out), .en(not_1_out), .Q(ALU_op_out), .clk(CLK));  // open: clr
  not not_1 (not_1_out, halt);
endmodule

module EX_MEM (
  input  [31:0] IR_in,
  input  [31:0] PC_in,
  input  [31:0] RS1_in,
  input  [31:0] RS2_in,
  input  [31:0] UImm_in,
  input  [31:0] ALU_result_in,
  input  NeedLink_in,
  input  RegWrite_in,
  input  MemWrite_in,
  input  [4:0] RegWriteNum_in,
  input  lui_in,
  input  ecall_in,
  input  sh_in,
  input  Mem2Reg_in,
  input  CLK,
  input  halt,
  output [31:0] IR_out,
  output [31:0] PC_out,
  output [31:0] RS1_out,
  output [31:0] RS2_out,
  output [31:0] UImm_out,
  output [31:0] ALU_result_out,
  output NeedLink_out,
  output RegWrite_out,
  output MemWrite_out,
  output [4:0] RegWriteNum_out,
  output lui_out,
  output ecall_out,
  output sh_out,
  output Mem2Reg_out
);

  wire not_1_out;

  Register #(.width(32), .trigger("rising"), .Select("low")) register_1 (
    .D(IR_in), .en(not_1_out), .Q(IR_out), .clk(CLK));  // open: clr
  Register #(.width(32), .trigger("rising"), .Select("low")) register_2 (
    .D(PC_in), .en(not_1_out), .Q(PC_out), .clk(CLK));  // open: clr
  Register #(.width(32), .trigger("rising"), .Select("low")) register_3 (
    .D(RS1_in), .en(not_1_out), .Q(RS1_out), .clk(CLK));  // open: clr
  Register #(.width(32), .trigger("rising"), .Select("low")) register_4 (
    .D(RS2_in), .en(not_1_out), .Q(RS2_out), .clk(CLK));  // open: clr
  Register #(.width(32), .trigger("rising"), .Select("low")) register_5 (
    .D(UImm_in), .en(not_1_out), .Q(UImm_out), .clk(CLK));  // open: clr
  Register #(.width(32), .trigger("rising"), .Select("low")) register_6 (
    .D(ALU_result_in), .en(not_1_out), .Q(ALU_result_out), .clk(CLK));  // open: clr
  Register #(.width(1), .trigger("rising"), .Select("low")) register_7 (
    .D(NeedLink_in), .en(not_1_out), .Q(NeedLink_out), .clk(CLK));  // open: clr
  Register #(.width(1), .trigger("rising"), .Select("low")) register_8 (
    .D(RegWrite_in), .en(not_1_out), .Q(RegWrite_out), .clk(CLK));  // open: clr
  Register #(.width(1), .trigger("rising"), .Select("low")) register_9 (
    .D(MemWrite_in), .en(not_1_out), .Q(MemWrite_out), .clk(CLK));  // open: clr
  Register #(.width(5), .trigger("rising"), .Select("low")) register_10 (
    .D(RegWriteNum_in), .en(not_1_out), .Q(RegWriteNum_out), .clk(CLK));  // open: clr
  Register #(.width(1), .trigger("rising"), .Select("low")) register_11 (
    .D(lui_in), .en(not_1_out), .Q(lui_out), .clk(CLK));  // open: clr
  Register #(.width(1), .trigger("rising"), .Select("low")) register_12 (
    .D(ecall_in), .en(not_1_out), .Q(ecall_out), .clk(CLK));  // open: clr
  Register #(.width(1), .trigger("rising"), .Select("low")) register_13 (
    .D(sh_in), .en(not_1_out), .Q(sh_out), .clk(CLK));  // open: clr
  Register #(.width(1), .trigger("rising"), .Select("low")) register_14 (
    .D(Mem2Reg_in), .en(not_1_out), .Q(Mem2Reg_out), .clk(CLK));  // open: clr
  not not_1 (not_1_out, halt);
endmodule

module MEM_WB (
  input  [31:0] IR_in,
  input  [31:0] PC_in,
  input  [31:0] RS1_in,
  input  [31:0] RS2_out,
  input  [31:0] MemData_in,
  input  [31:0] RegData_in,
  input  MemWrite_in,
  input  [31:0] MemWriteAddr_in,
  input  RegWrite_in,
  input  [4:0] RegWriteNum_in,
  input  ecall_in,
  input  CLK,
  input  halt,
  output [31:0] IR_out,
  output [31:0] PC_out,
  output [31:0] RS1_out,
  output [31:0] RS2_out_2,
  output [31:0] MemData_out,
  output [31:0] RegData_out,
  output MemWrite_out,
  output [31:0] MemWriteAddr_out,
  output RegWrite_out,
  output [4:0] RegWriteNum_out,
  output ecall_out
);

  wire not_1_out;

  Register #(.width(32), .trigger("rising"), .Select("low")) register_1 (
    .D(IR_in), .en(not_1_out), .Q(IR_out), .clk(CLK));  // open: clr
  Register #(.width(32), .trigger("rising"), .Select("low")) register_2 (
    .D(PC_in), .en(not_1_out), .Q(PC_out), .clk(CLK));  // open: clr
  Register #(.width(32), .trigger("rising"), .Select("low")) register_3 (
    .D(RS1_in), .en(not_1_out), .Q(RS1_out), .clk(CLK));  // open: clr
  Register #(.width(32), .trigger("rising"), .Select("low")) register_4 (
    .D(RS2_out), .en(not_1_out), .Q(RS2_out_2), .clk(CLK));  // open: clr
  Register #(.width(32), .trigger("rising"), .Select("low")) register_5 (
    .D(MemData_in), .en(not_1_out), .Q(MemData_out), .clk(CLK));  // open: clr
  Register #(.width(32), .trigger("rising"), .Select("low")) register_6 (
    .D(RegData_in), .en(not_1_out), .Q(RegData_out), .clk(CLK));  // open: clr
  Register #(.width(1), .trigger("rising"), .Select("low")) register_7 (
    .D(MemWrite_in), .en(not_1_out), .Q(MemWrite_out), .clk(CLK));  // open: clr
  Register #(.width(32), .trigger("rising"), .Select("low")) register_8 (
    .D(MemWriteAddr_in), .en(not_1_out), .Q(MemWriteAddr_out), .clk(CLK));  // open: clr
  Register #(.width(1), .trigger("rising"), .Select("low")) register_9 (
    .D(RegWrite_in), .en(not_1_out), .Q(RegWrite_out), .clk(CLK));  // open: clr
  Register #(.width(5), .trigger("rising"), .Select("low")) register_10 (
    .D(RegWriteNum_in), .en(not_1_out), .Q(RegWriteNum_out), .clk(CLK));  // open: clr
  Register #(.width(1), .trigger("rising"), .Select("low")) register_11 (
    .D(ecall_in), .en(not_1_out), .Q(ecall_out), .clk(CLK));  // open: clr
  not not_1 (not_1_out, halt);
endmodule

module \ID_EX_for_重定向  (
  input  [31:0] IRin,
  input  [31:0] PCin,
  input  [31:0] RS1in,
  input  [31:0] RS2in,
  input  [31:0] Imm_in,
  input  RegWrite_in,
  input  MemWrite_in,
  input  [4:0] RegWriteNum_in,
  input  ALU_src_in,
  input  jal_in,
  input  jalr_in,
  input  beq_in,
  input  bne_in,
  input  bge_in,
  input  sh_in,
  input  lui_in,
  input  ecall_in,
  input  Mem2Reg_in,
  input  [31:0] BImm_in,
  input  [31:0] UImm_in,
  input  [31:0] JImm_in,
  input  [3:0] ALI_op_in,
  input  [1:0] R1_fwd,
  input  [1:0] R2_fwd,
  input  CLK,
  input  halt,
  input  clear,
  output [31:0] IRout,
  output [31:0] PCout,
  output [31:0] RS1out,
  output [31:0] RS2out,
  output [31:0] Imm_out,
  output RegWrite_out,
  output MemWrite_out,
  output [4:0] RegWriteNum_out,
  output ALU_src_out,
  output jal_out,
  output jalr_out,
  output beq_out,
  output bne_out,
  output bge_out,
  output sh_out,
  output lui_out,
  output ecall_out,
  output Mem2Reg_out,
  output [31:0] BImm_out,
  output [31:0] UImm_out,
  output [31:0] JImm_out,
  output [3:0] ALU_op_out,
  output [1:0] R1_fwd_2,
  output [1:0] R2_fwd_2
);

  wire multiplexer_1_out, multiplexer_2_out, multiplexer_3_out, multiplexer_4_out, multiplexer_10_out,
       multiplexer_11_out, multiplexer_13_out, multiplexer_14_out, multiplexer_15_out, multiplexer_16_out,
       multiplexer_17_out, multiplexer_18_out, not_1_out;
  wire [1:0] multiplexer_23_out, multiplexer_24_out;
  wire [3:0] multiplexer_22_out;
  wire [4:0] multiplexer_12_out;
  wire [31:0] multiplexer_5_out, multiplexer_6_out, multiplexer_7_out, multiplexer_8_out, multiplexer_9_out,
       multiplexer_19_out, multiplexer_20_out, multiplexer_21_out;

  Multiplexer #(.select(1), .width(1), .disabled("Z"), .enable("false")) multiplexer_1 (
    .in0(ALU_src_in), .in1(1'b0), .out(multiplexer_1_out), .sel(clear));
  Multiplexer #(.select(1), .width(1), .disabled("Z"), .enable("false")) multiplexer_2 (
    .in0(beq_in), .in1(1'b0), .out(multiplexer_2_out), .sel(clear));
  Multiplexer #(.select(1), .width(1), .disabled("Z"), .enable("false")) multiplexer_3 (
    .in0(bne_in), .in1(1'b0), .out(multiplexer_3_out), .sel(clear));
  Multiplexer #(.select(1), .width(1), .disabled("Z"), .enable("false")) multiplexer_4 (
    .in0(bge_in), .in1(1'b0), .out(multiplexer_4_out), .sel(clear));
  Multiplexer #(.select(1), .width(32), .disabled("Z"), .enable("false")) multiplexer_5 (
    .in0(IRin), .in1({32{1'b0}}), .out(multiplexer_5_out), .sel(clear));
  Multiplexer #(.select(1), .width(32), .disabled("Z"), .enable("false")) multiplexer_6 (
    .in0(PCin), .in1({32{1'b0}}), .out(multiplexer_6_out), .sel(clear));
  Multiplexer #(.select(1), .width(32), .disabled("Z"), .enable("false")) multiplexer_7 (
    .in0(RS1in), .in1({32{1'b0}}), .out(multiplexer_7_out), .sel(clear));
  Multiplexer #(.select(1), .width(32), .disabled("Z"), .enable("false")) multiplexer_8 (
    .in0(RS2in), .in1({32{1'b0}}), .out(multiplexer_8_out), .sel(clear));
  Multiplexer #(.select(1), .width(32), .disabled("Z"), .enable("false")) multiplexer_9 (
    .in0(Imm_in), .in1({32{1'b0}}), .out(multiplexer_9_out), .sel(clear));
  Multiplexer #(.select(1), .width(1), .disabled("Z"), .enable("false")) multiplexer_10 (
    .in0(RegWrite_in), .in1(1'b0), .out(multiplexer_10_out), .sel(clear));
  Multiplexer #(.select(1), .width(1), .disabled("Z"), .enable("false")) multiplexer_11 (
    .in0(MemWrite_in), .in1(1'b0), .out(multiplexer_11_out), .sel(clear));
  Multiplexer #(.select(1), .width(5), .disabled("Z"), .enable("false")) multiplexer_12 (
    .in0(RegWriteNum_in), .in1({5{1'b0}}), .out(multiplexer_12_out), .sel(clear));
  Multiplexer #(.select(1), .width(1), .disabled("Z"), .enable("false")) multiplexer_13 (
    .in0(jal_in), .in1(1'b0), .out(multiplexer_13_out), .sel(clear));
  Multiplexer #(.select(1), .width(1), .disabled("Z"), .enable("false")) multiplexer_14 (
    .in0(jalr_in), .in1(1'b0), .out(multiplexer_14_out), .sel(clear));
  Multiplexer #(.select(1), .width(1), .disabled("Z"), .enable("false")) multiplexer_15 (
    .in0(sh_in), .in1(1'b0), .out(multiplexer_15_out), .sel(clear));
  Multiplexer #(.select(1), .width(1), .disabled("Z"), .enable("false")) multiplexer_16 (
    .in0(lui_in), .in1(1'b0), .out(multiplexer_16_out), .sel(clear));
  Multiplexer #(.select(1), .width(1), .disabled("Z"), .enable("false")) multiplexer_17 (
    .in0(ecall_in), .in1(1'b0), .out(multiplexer_17_out), .sel(clear));
  Multiplexer #(.select(1), .width(1), .disabled("Z"), .enable("false")) multiplexer_18 (
    .in0(Mem2Reg_in), .in1(1'b0), .out(multiplexer_18_out), .sel(clear));
  Multiplexer #(.select(1), .width(32), .disabled("Z"), .enable("false")) multiplexer_19 (
    .in0(BImm_in), .in1({32{1'b0}}), .out(multiplexer_19_out), .sel(clear));
  Multiplexer #(.select(1), .width(32), .disabled("Z"), .enable("false")) multiplexer_20 (
    .in0(UImm_in), .in1({32{1'b0}}), .out(multiplexer_20_out), .sel(clear));
  Multiplexer #(.select(1), .width(32), .disabled("Z"), .enable("false")) multiplexer_21 (
    .in0(JImm_in), .in1({32{1'b0}}), .out(multiplexer_21_out), .sel(clear));
  Multiplexer #(.select(1), .width(4), .disabled("Z"), .enable("false")) multiplexer_22 (
    .in0(ALI_op_in), .in1(4'b0000), .out(multiplexer_22_out), .sel(clear));
  Multiplexer #(.select(1), .width(2), .disabled("Z"), .enable("false")) multiplexer_23 (
    .in0(R1_fwd), .in1(2'b00), .out(multiplexer_23_out), .sel(clear));
  Multiplexer #(.select(1), .width(2), .disabled("Z"), .enable("false")) multiplexer_24 (
    .in0(R2_fwd), .in1(2'b00), .out(multiplexer_24_out), .sel(clear));
  Register #(.width(32), .trigger("rising"), .Select("low")) register_1 (
    .D(multiplexer_5_out), .en(not_1_out), .Q(IRout), .clk(CLK));  // open: clr
  Register #(.width(32), .trigger("rising"), .Select("low")) register_2 (
    .D(multiplexer_6_out), .en(not_1_out), .Q(PCout), .clk(CLK));  // open: clr
  Register #(.width(32), .trigger("rising"), .Select("low")) register_3 (
    .D(multiplexer_7_out), .en(not_1_out), .Q(RS1out), .clk(CLK));  // open: clr
  Register #(.width(32), .trigger("rising"), .Select("low")) register_4 (
    .D(multiplexer_8_out), .en(not_1_out), .Q(RS2out), .clk(CLK));  // open: clr
  Register #(.width(32), .trigger("rising"), .Select("low")) register_5 (
    .D(multiplexer_9_out), .en(not_1_out), .Q(Imm_out), .clk(CLK));  // open: clr
  Register #(.width(1), .trigger("rising"), .Select("low")) register_6 (
    .D(multiplexer_10_out), .en(not_1_out), .Q(RegWrite_out), .clk(CLK));  // open: clr
  Register #(.width(1), .trigger("rising"), .Select("low")) register_7 (
    .D(multiplexer_11_out), .en(not_1_out), .Q(MemWrite_out), .clk(CLK));  // open: clr
  Register #(.width(5), .trigger("rising"), .Select("low")) register_8 (
    .D(multiplexer_12_out), .en(not_1_out), .Q(RegWriteNum_out), .clk(CLK));  // open: clr
  Register #(.width(1), .trigger("rising"), .Select("low")) register_9 (
    .D(multiplexer_1_out), .en(not_1_out), .Q(ALU_src_out), .clk(CLK));  // open: clr
  Register #(.width(1), .trigger("rising"), .Select("low")) register_10 (
    .D(multiplexer_13_out), .en(not_1_out), .Q(jal_out), .clk(CLK));  // open: clr
  Register #(.width(1), .trigger("rising"), .Select("low")) register_11 (
    .D(multiplexer_14_out), .en(not_1_out), .Q(jalr_out), .clk(CLK));  // open: clr
  Register #(.width(1), .trigger("rising"), .Select("low")) register_12 (
    .D(multiplexer_2_out), .en(not_1_out), .Q(beq_out), .clk(CLK));  // open: clr
  Register #(.width(1), .trigger("rising"), .Select("low")) register_13 (
    .D(multiplexer_3_out), .en(not_1_out), .Q(bne_out), .clk(CLK));  // open: clr
  Register #(.width(1), .trigger("rising"), .Select("low")) register_14 (
    .D(multiplexer_4_out), .en(not_1_out), .Q(bge_out), .clk(CLK));  // open: clr
  Register #(.width(1), .trigger("rising"), .Select("low")) register_15 (
    .D(multiplexer_15_out), .en(not_1_out), .Q(sh_out), .clk(CLK));  // open: clr
  Register #(.width(1), .trigger("rising"), .Select("low")) register_16 (
    .D(multiplexer_16_out), .en(not_1_out), .Q(lui_out), .clk(CLK));  // open: clr
  Register #(.width(1), .trigger("rising"), .Select("low")) register_17 (
    .D(multiplexer_17_out), .en(not_1_out), .Q(ecall_out), .clk(CLK));  // open: clr
  Register #(.width(1), .trigger("rising"), .Select("low")) register_18 (
    .D(multiplexer_18_out), .en(not_1_out), .Q(Mem2Reg_out), .clk(CLK));  // open: clr
  Register #(.width(32), .trigger("rising"), .Select("low")) register_19 (
    .D(multiplexer_19_out), .en(not_1_out), .Q(BImm_out), .clk(CLK));  // open: clr
  Register #(.width(32), .trigger("rising"), .Select("low")) register_20 (
    .D(multiplexer_20_out), .en(not_1_out), .Q(UImm_out), .clk(CLK));  // open: clr
  Register #(.width(32), .trigger("rising"), .Select("low")) register_21 (
    .D(multiplexer_21_out), .en(not_1_out), .Q(JImm_out), .clk(CLK));  // open: clr
  Register #(.width(4), .trigger("rising"), .Select("low")) register_22 (
    .D(multiplexer_22_out), .en(not_1_out), .Q(ALU_op_out), .clk(CLK));  // open: clr
  Register #(.width(2), .trigger("rising"), .Select("low")) register_23 (
    .D(multiplexer_23_out), .en(not_1_out), .Q(R1_fwd_2), .clk(CLK));  // open: clr
  Register #(.width(2), .trigger("rising"), .Select("low")) register_24 (
    .D(multiplexer_24_out), .en(not_1_out), .Q(R2_fwd_2), .clk(CLK));  // open: clr
  not not_1 (not_1_out, halt);
endmodule
